// Digital circuit assembler.dig as structural Verilog
module assembler (
  input  prog,
  input  [7:0] value,
  input  [1:0] dest,
  input  [1:0] src,
  input  tworeg,
  input  add,
  input  move,
  input  jump,
  output [15:0] inst,
  output store_clk
);

  wire priorityencoder_1_any;

  PriorityEncoder #(.Selector_Bits(3)) priorityencoder_1 (
    .in0(add), .in1(1'b0), .in2(1'b0), .in3(1'b0), .in4(1'b0), .in5(1'b0), .in6(move), .in7(jump),
    .num(inst[3:1]), .any(priorityencoder_1_any));
  and and_1 (store_clk, priorityencoder_1_any, prog);

  assign {inst[15:4], inst[0]} = {value, src, dest, tworeg};

  // Notes on the sheet:
  //   value: default 100
  //   dest: default 1
  //   src: default 1
  //   tworeg: default 1
  //   add: default 100
endmodule
