// Digital circuit bin2bcd.dig as structural Verilog
module bin2bcd (
  input  [15:0] I,
  output [19:0] O
);

  wire [15:0] div_1_q, div_2_q, div_3_q, div_4_q;
  wire [15:4] div_1_r, div_2_r, div_3_r, div_4_r, div_5_r;

  Div #(.Bits(16)) div_1 (.a(I), .b(16'ha), .q(div_1_q), .r({div_1_r, O[3:0]}));
  Div #(.Bits(16)) div_2 (.a(div_1_q), .b(16'ha), .q(div_2_q), .r({div_2_r, O[7:4]}));
  Div #(.Bits(16)) div_3 (.a(div_2_q), .b(16'ha), .q(div_3_q), .r({div_3_r, O[11:8]}));
  Div #(.Bits(16)) div_4 (.a(div_3_q), .b(16'ha), .q(div_4_q), .r({div_4_r, O[15:12]}));
  Div #(.Bits(16)) div_5 (.a(div_4_q), .b(16'ha), .r({div_5_r, O[19:16]}));  // open: q
endmodule
