// Digital circuit busdisplay.dig as structural Verilog
module busdisplay (
  input  [33:0] i,
  input  H,
  input  [1:0] S,
  input  [63:0] B,
  output [3:0] D1,
  output P1,
  output [3:0] D2,
  output P2,
  output [33:0] o,
  output [3:0] D3,
  output P3,
  output [3:0] D4,
  output P4,
  output [3:0] D5,
  output P5
);

  wire aluop2ascii_1_l_v, aluop2ascii_1_r_v, aluop2ascii_1_res_v, imm_v, multiplexer_2_out;
  wire [2:0] aluop_t;
  wire [15:0] multiplexer_1_out;

  // ctrlbreakout ctrlbreakout_1: pin names not known; wires that end beside it: i, imm_v, aluop_t
  Multiplexer #(.Selector_Bits(2), .Bits(16)) multiplexer_1 (
    .sel(S), .in_0(B[63:48]), .in_1(B[15:0]), .in_2(B[31:16]), .in_3(B[47:32]), .out(multiplexer_1_out));
  hexdisplay hexdisplay_1 (
    .D1(D1), .P1(P1), .D2(D2), .P2(P2), .D3(D3), .P3(P3), .D4(D4), .P4(P4), .D5(D5), .P5(P5),
    .E(multiplexer_2_out), .V(multiplexer_1_out), .H(H));
  aluop2ascii aluop2ascii_1 (
    .I({1'b0, aluop_t}), .L_v(aluop2ascii_1_l_v), .R_v(aluop2ascii_1_r_v), .res_v(aluop2ascii_1_res_v));  // open: L0, L1, L2, L3
  Multiplexer #(.Selector_Bits(2)) multiplexer_2 (
    .sel(S), .in_0(imm_v), .in_1(aluop2ascii_1_l_v), .in_2(aluop2ascii_1_r_v), .in_3(aluop2ascii_1_res_v),
    .out(multiplexer_2_out));

  assign o = i;

  // Other names for the same wires on the sheet: l_t[15:0] = B[15:0]; r_t[15:0] = B[31:16]; res_t[15:0] = B[47:32];
  //   imm_t[15:0] = B[63:48]
endmodule
