// Digital circuit bussplitter.dig as structural Verilog
module bussplitter (
  input  [7:0] address,
  input  [3:0] sel,
  input  [15:0] in_0,
  input  [15:0] in_1,
  input  [15:0] in_2,
  input  [15:0] in_3,
  input  [15:0] bus_in,
  output [15:0] bus_out,
  output [1:0] subaddress
);

  wire active_eq;
  wire [15:0] multiplexer_1_out;

  Comparator #(.Bits(4)) active (.a(address[7:4]), .b(sel), .eq(active_eq));  // open: gt, lt
  Multiplexer #(.Selector_Bits(2), .Bits(16)) multiplexer_1 (
    .sel(address[3:2]), .in_0(in_0), .in_1(in_1), .in_2(in_2), .in_3(in_3), .out(multiplexer_1_out));
  Multiplexer #(.Bits(16)) multiplexer_2 (.sel(active_eq), .in_0(bus_in), .in_1(multiplexer_1_out), .out(bus_out));

  assign subaddress = address[1:0];
endmodule
