// Digital circuit clockctrl.dig as structural Verilog
module clockctrl (
  input  clock,
  input  step,
  input  run,
  output stall
);

  wire and_1_out, d_ff_1_nq, d_ff_as_1_q, d_ff_as_2_q, or_1_out, or_2_out;
  wire [22:0] counter_1_out;

  or or_1 (or_1_out, counter_1_out[22], step);
  D_FF_AS d_ff_as_1 (.Set(or_1_out), .D(1'b0), .C(clock), .Clr(1'b0), .Q(d_ff_as_1_q));  // open: nQ
  D_FF d_ff_1 (.D(d_ff_as_1_q), .C(clock), .nQ(d_ff_1_nq));  // open: Q
  and and_1 (and_1_out, d_ff_as_1_q, d_ff_1_nq);
  or or_2 (or_2_out, d_ff_as_2_q, run);
  D_FF_AS d_ff_as_2 (.Set(1'b0), .D(or_2_out), .C(clock), .Clr(step), .Q(d_ff_as_2_q));  // open: nQ
  Counter #(.Bits(23)) counter_1 (.en(d_ff_as_2_q), .C(clock), .clr(step), .out(counter_1_out));  // open: ovf
  D_FF d_ff_2 (.D(and_1_out), .C(clock), .nQ(stall));  // open: Q
endmodule
