// Digital circuit datamemio.dig as structural Verilog
module datamemio (
  input  we,
  input  [15:0] A,
  input  [15:0] D_in,
  input  [15:0] D_out,
  input  req,
  input  ack,
  input  clk
);

  wire ack2, and_1_out, and_2_out, d_ff_2_q, req1, req2, req3, req4, telnet_1_av;
  wire [7:0] d_ff_1_q, telnet_1_out;
  wire [15:0] Data_d;

  and and_1 (and_1_out, req2, we);
  and and_2 (and_2_out, req2, ~we, telnet_1_av);  // And
  or or_1 (ack2, and_1_out, and_2_out);
  BlockRAMDualPort #(.AddrBits(14), .Bits(16)) Data (.A(A[13:0]), .Din(D_in), .str(we), .C(clk), .D(Data_d));
  Telnet #(.port(2323)) telnet_1 (
    .in(D_in[7:0]), .C(clk), .wr(and_1_out), .rd(and_2_out), .out(telnet_1_out), .av(telnet_1_av));
  D_FF #(.Bits(8)) d_ff_1 (.D(telnet_1_out), .C(clk), .Q(d_ff_1_q));  // open: nQ
  Multiplexer #(.Selector_Bits(2), .Bits(16)) multiplexer_1 (
    .sel(A[15:14]), .in_0(Data_d), .in_1({{8{1'b0}}, d_ff_1_q}), .in_2({16{1'b0}}), .in_3({16{1'b0}}),
    .out(D_out));
  Demultiplexer #(.Selector_Bits(2)) demultiplexer_1 (
    .sel(A[15:14]), .in(req), .out_0(req1), .out_1(req2), .out_2(req3), .out_3(req4));
  D_FF d_ff_2 (.D(req), .C(clk), .Q(d_ff_2_q));  // open: nQ
  Multiplexer #(.Selector_Bits(2)) multiplexer_2 (
    .sel(A[15:14]), .in_0(d_ff_2_q), .in_1(ack2), .in_2(1'b1), .in_3(1'b1), .out(ack));

  // Other names for the same wires on the sheet: C = clk
endmodule
