// Digital circuit debugbus.dig as structural Verilog
module debugbus (
  input  db_ready,
  input  clock,
  input  [15:0] ctrl,
  input  [15:0] decode,
  input  [15:0] wrval,
  input  [15:0] result,
  input  [15:0] L,
  input  [15:0] R,
  input  [15:0] imm,
  input  [15:0] pc,
  output [25:0] db
);

  wire debugregs_1_ready_out, debugregs_1_valid_out;
  wire [7:0] Addr_Enumerator_out, debugregs_1_addr_out;
  wire [15:0] debugregs_1_data_out;

  Counter #(.Bits(8)) Addr_Enumerator (
    .en(db_ready), .C(clock), .clr(~db[16]), .out(Addr_Enumerator_out));  // open: ovf
  debugregs debugregs_1 (
    .data_in({16{1'b0}}), .valid_in(1'b0), .addr_in(Addr_Enumerator_out), .ready_in(db_ready),
    .write(ctrl[10]), .en(ctrl[12]), .clock(clock), .rd(decode[3:0]), .wrval(wrval), .sel({8{1'b0}}),
    .data_out(debugregs_1_data_out), .valid_out(debugregs_1_valid_out), .addr_out(debugregs_1_addr_out),
    .ready_out(debugregs_1_ready_out));
  debugmux debugmux_1 (
    .data_in(debugregs_1_data_out), .valid_in(debugregs_1_valid_out), .addr_in(debugregs_1_addr_out),
    .ready_in(debugregs_1_ready_out), .sel(8'h10), .in_0(decode), .in_1(ctrl), .in_2(L), .in_3(R),
    .in_4(result), .in_5(wrval), .in_6(imm), .in_7(pc), .data_out(db[15:0]), .valid_out(db[16]),
    .addr_out(db[24:17]));  // open: ready_out

  assign db[25] = clock;

  // Other names for the same wires on the sheet: C = clock

  // Notes on the sheet:
  //   clock: Hz: 2
  //   Memory Map:
  //   00-0F: registers
  //   10: decode
  //   11: ctrl
  //   12: L
  //   13: R
  //   14: result
  //   15: wrval
  //   16: imm
  //   17: pc
endmodule
