// Digital circuit debugcopy.dig as structural Verilog
module debugcopy (
  input  [25:0] db,
  input  clock,
  input  e,
  output [15:0] R0,
  output [15:0] R1,
  output [15:0] R2,
  output [15:0] R3,
  output [15:0] decode,
  output [15:0] ctrl,
  output [15:0] L,
  output [15:0] R,
  output [15:0] result,
  output [15:0] imm,
  output [15:0] pc
);

  wire [24:0] register_1_q, register_2_q, register_3_q;

  Register #(.Bits(25)) register_1 (.D(db[24:0]), .C(db[25]), .en(1'b1), .Q(register_1_q));
  Register #(.Bits(25)) register_2 (.D(register_1_q), .C(clock), .en(1'b1), .Q(register_2_q));
  Register #(.Bits(25)) register_3 (.D(register_2_q), .C(clock), .en(1'b1), .Q(register_3_q));
  debugregcopy debugregcopy_1 (
    .o0(R0), .o1(R1), .o2(R2), .o3(R3), .db({clock, register_3_q}), .b({5{1'b0}}), .e(e));  // open: o4, o5, o6, o7
  debugregcopy debugregcopy_2 (
    .o0(decode), .o1(ctrl), .o2(L), .o3(R), .o5(result), .o6(imm), .o7(pc), .db({clock, register_3_q}),
    .b(5'b00010), .e(e));  // open: o4

  // Other names for the same wires on the sheet: C = clock
endmodule
