// Digital circuit debugreg.dig as structural Verilog
module debugreg (
  input  [38:0] i,
  input  [4:0] s,
  input  [38:0] o,
  output [15:0] v
);

  wire and_1_out, comparator_1_eq;
  wire [15:0] register_1_q;

  Comparator #(.Bits(4)) comparator_1 (.a(i[19:16]), .b(s[3:0]), .eq(comparator_1_eq));  // open: gt, lt
  and and_1 (and_1_out, i[21], i[20], comparator_1_eq);
  Register #(.Bits(16)) register_1 (.D(i[15:0]), .C(i[38]), .en(and_1_out), .Q(register_1_q));
  Multiplexer #(.Bits(16)) multiplexer_1 (.sel(s[4]), .in_0(register_1_q), .in_1(i[37:22]), .out(v));

  assign o = i;

  // Other names for the same wires on the sheet: wrval_t[15:0] = i[15:0]; rd_t[3:0] = i[19:16]; en = i[20];
  //   write_t = i[21]; PC_t[15:0] = i[37:22]; C = i[38]
endmodule
