// Digital circuit decodedec.dig as structural Verilog
module decodedec (
  input  [15:0] D,
  output [3:0] r,
  output pc,
  output valid
);


  assign pc = D[4];
  assign r = D[3:0];
  assign valid = D[5];
endmodule
