// Digital circuit decoder.dig as structural Verilog
module decoder (
  input  [15:0] rdval,
  input  [15:0] rsval,
  input  [15:0] instr,
  input  [15:0] pc,
  input  jump,
  input  clk,
  input  en,
  output [3:0] rs,
  output [3:0] rd,
  output [15:0] L,
  output [15:0] R,
  output [4:0] op,
  output rs_valid,
  output rd_valid,
  output [15:0] imm,
  output immv
);

  wire i11, imm_do, imm_op, imm_valid, mem, register_1_q;
  wire [11:0] Imm_q, multiplexer_2_out;
  wire [15:0] imm6, imm8, imm11, multiplexer_1_out, multiplexer_4_out, multiplexer_7_out;

  BitExtender #(.inputBits(6)) bitextender_1 (.in(instr[11:6]), .out(imm6));
  BitExtender bitextender_2 (.in(instr[11:4]), .out(imm8));
  BitExtender #(.inputBits(11)) bitextender_3 (.in(instr[15:5]), .out(imm11));
  Multiplexer #(.Bits(16)) multiplexer_1 (.sel(i11), .in_0(imm8), .in_1(imm11), .out(multiplexer_1_out));
  Register #(.Bits(12)) u_Imm (.D(instr[15:4]), .C(clk), .en(imm_do), .Q(Imm_q));
  Multiplexer #(.Selector_Bits(2), .Bits(16)) multiplexer_2 (
    .sel(instr[1:0]), .in_0({16{1'b0}}), .in_1(multiplexer_1_out), .in_2({{12{1'b0}}, instr[7:4]}),
    .in_3(imm6), .out({multiplexer_2_out, imm[3:0]}));
  Register register_1 (.D(imm_do), .C(clk), .en(en), .Q(register_1_q));
  instdecoder instdecoder_1 (
    .fmt(instr[1:0]), .op0(instr[6:2]), .op(op), .rd_valid(rd_valid), .rs_valid(rs_valid),
    .imm_valid(imm_valid), .mem(mem), .i11(i11), .imm_op(imm_op));
  Multiplexer #(.Bits(12)) multiplexer_3 (.sel(register_1_q), .in_0(multiplexer_2_out), .in_1(Imm_q), .out(imm[15:4]));
  and and_1 (imm_do, en, imm_op);
  or or_1 (immv, imm_valid, mem);
  Multiplexer #(.Bits(16)) multiplexer_4 (.sel(rs_valid), .in_0(pc), .in_1({16{1'b0}}), .out(multiplexer_4_out));
  Multiplexer #(.Bits(4)) multiplexer_5 (.sel(rs_valid), .in_0(4'b0000), .in_1(instr[11:8]), .out(rs));
  Multiplexer #(.Bits(4)) multiplexer_6 (.sel(rd_valid), .in_0(4'b0000), .in_1(instr[15:12]), .out(rd));
  Multiplexer #(.Bits(16)) multiplexer_7 (.sel(jump), .in_0(rdval), .in_1(multiplexer_4_out), .out(multiplexer_7_out));
  Multiplexer #(.Bits(16)) multiplexer_8 (.sel(imm_valid), .in_0(rsval), .in_1(imm), .out(R));
  Multiplexer #(.Bits(16)) multiplexer_9 (.sel(mem), .in_0(multiplexer_7_out), .in_1(imm), .out(L));

  // Other names for the same wires on the sheet: C = clk; en_t = en; fmt[1:0] = instr[1:0]; op0[4:0] = instr[6:2];
  //   off4[3:0] = instr[7:4]; rs_i[3:0] = instr[11:8]; rd_i[3:0] = instr[15:12]
endmodule

/* Test case ls:
instr               rsval rs rdval rd L       R  op       
0b0000000010100010  2     0  2     0  0b1010 2  0b01100  
0b0000000000000110  3     0  2     0  0b0000 3  0b01101  
0b1111000010011010  4     0  2    15  0b1001 4  0b01110  
0b0000111110011110  5    15  2     0  0b1001 5  0b01111  
   
*/

/* Test case rr:
instr               rsval rs rdval rd L R op 
0b0000000000000000  5     0  2     0  2 5 0b00000  
0b0011000001111100  5     0  2     3  2 5 31 
0b0011001101000000  5     3  2     3  2 5 16 
*/

/* Test case ri8:
instr               rsval rs rdval rd L R      op       
0b0000000000000001  5     0  1     0  1 0      0b00110  
0b1111000011111001  5     0  2    15  2 0xf    0b00111  
0b0011111100010001  5     0  3     3  3 0xfff1 0b00110  
0b0010011110111001  5     0  4     2  4 0x7b   0b00111  
*/

/* Test case i11:
instr               rsval rs rdval rd L R      op       
0b0000000000000101  5     0  2     0  2 0      0b01000   
0b0000000000100101  5     0  2     0  2 1      0b01000  
0b0100000000110101  5     0  2     0  2 0x201  0b01010   
0b1111111110110101  5     0  2     0  2 0xFFFD 0b01010  
 
*/

/* Test case ri6:
instr               rsval rs rdval rd L R      op       
0b0000000000000011  5     0  1     0  1 0      0b10000  
0b1111000011011111  5     0  2    15  2 3      0b10111  
0b0011110001001011  5     0  3     3  3 0xfff1 0b10010  
0b0010000101011011  5     0  4     2  4 5      0b10110  
*/
