// Digital circuit execute.dig as structural Verilog
module execute (
  input  [15:0] L,
  input  [15:0] R,
  input  [2:0] cond,
  input  [2:0] op,
  output [15:0] result,
  output skip_n
);

  wire and_1_out, and_3_out, and_4_out, and_5_out, and_6_out, and_7_out, and_8_out, and_9_out, and_10_out, C,
       eq, eq_eq, ge, hs, lo, lt, N, ne, not_2_out, not_3_out, not_4_out, RN, V, xor_2_out;
  wire [14:0] add_1_s, multiplexer_1_out;
  wire [15:0] and_2_out, not_1_out, or_1_out, \xor ;

  and and_1 (and_1_out, op[1], ~op[2]);  // And
  Decoder #(.Selector_Bits(3)) decoder_1 (
    .sel(cond), .out_1(eq), .out_2(ne), .out_3(lt), .out_4(ge), .out_5(lo), .out_6(hs));  // open: out_0, out_7
  Multiplexer #(.Bits(16)) multiplexer_1 (.sel(and_1_out), .in_0(R), .in_1(not_1_out), .out({RN, multiplexer_1_out}));
  assign not_1_out = ~R;  // Not not_1, 16 bits wide
  Add #(.Bits(16)) add_1 (.a(L), .b({RN, multiplexer_1_out}), .c_i(and_1_out), .s({N, add_1_s}), .c_o(C));
  assign \xor  = L ^ R;  // XOr xor_1, 16 bits wide
  assign and_2_out = L & R;  // And and_2, 16 bits wide
  assign or_1_out = L | R;  // Or or_1, 16 bits wide
  Comparator #(.Bits(16)) u_eq (.a(\xor ), .b({16{1'b0}}), .eq(eq_eq));  // open: gt, lt
  and and_3 (and_3_out, L[15], RN, ~N);  // And
  and and_4 (and_4_out, ~L[15], ~RN, N);  // And
  xor xor_2 (xor_2_out, N, V);
  or or_2 (V, and_3_out, and_4_out);
  not not_2 (not_2_out, xor_2_out);
  not not_3 (not_3_out, C);
  not not_4 (not_4_out, eq_eq);
  Multiplexer #(.Selector_Bits(3), .Bits(16)) multiplexer_2 (
    .sel(op), .in_0(L), .in_1({N, add_1_s}), .in_2(L), .in_3({N, add_1_s}), .in_4(R), .in_5(\xor ),
    .in_6(and_2_out), .in_7(or_1_out), .out(result));
  and and_5 (and_5_out, lt, not_2_out);
  and and_6 (and_6_out, ge, xor_2_out);
  and and_7 (and_7_out, lo, C);
  and and_8 (and_8_out, hs, not_3_out);
  and and_9 (and_9_out, ne, eq_eq);
  and and_10 (and_10_out, eq, not_4_out);
  or or_3 (skip_n, and_5_out, and_6_out, and_7_out, and_8_out, and_9_out, and_10_out);

  // Other names for the same wires on the sheet: LN = L[15]
endmodule
