// Digital circuit frontpanel.dig as structural Verilog
module frontpanel (
  input  clock,
  input  erun,
  output [15:0] RA,
  output [15:0] R1_a0,
  output [15:0] R2_a1,
  output [15:0] R3_a2,
  output [15:0] PC,
  output halt,
  output error,
  output [15:0] R4_s0,
  output [15:0] R5_s1,
  output [15:0] R6_s2,
  output [15:0] R7_s3,
  output [15:0] R8_t0,
  output [15:0] R9_t1,
  output [15:0] R10_t2,
  output [15:0] R11_t3,
  output [15:0] R12_t4,
  output [15:0] FP,
  output [15:0] BP,
  output [15:0] SP
);

  wire aluopdisplay_1_p1, aluopdisplay_1_p2, busdisplay_1_p3, busdisplay_1_p6, busdisplay_1_p9,
       busdisplay_1_p11, busdisplay_2_p1, busdisplay_2_p2, busdisplay_2_p3, busdisplay_2_p4, busdisplay_2_p5,
       busdisplay_3_p3, busdisplay_3_p6, busdisplay_3_p10, busdisplay_3_p12, busdisplay_3_p15,
       busdisplay_4_p1, busdisplay_4_p2, busdisplay_4_p3, busdisplay_4_p4, busdisplay_4_p5, ctrl, db,
       debugreg_1_p3, debugreg_2_p3, debugreg_3_p5, debugreg_4_p5, debugreg_6_p3, debugreg_7_p3,
       debugreg_8_p3, debugreg_9_p3, debugreg_10_p3, debugreg_12_p3, debugreg_13_p3, debugreg_14_p3,
       debugreg_15_p3, debugreg_16_p3, hex, instrdisplay_1_p3, instrdisplay_1_p5, instrdisplay_1_p7,
       instrdisplay_1_p9, instrdisplay_1_p11, instrdisplay_1_p13, MC, rddisplay_1_p3, rddisplay_1_p6,
       rddisplay_1_p8, rddisplay_1_p9, rddisplay_2_p1, rddisplay_2_p5, rddisplay_2_p6, rddisplay_2_p10,
       rddisplay_2_p12, rddisplay_2_p13, rddisplay_3_p3, rddisplay_3_p6, rddisplay_3_p8, rddisplay_3_p9,
       \reg , rj32_1_p5, rj32_1_p13, rj32_1_p15, run_t, skip, slow_t, stalled_t, step_t;
  wire [3:0] busdisplay_1_p2, busdisplay_1_p5, busdisplay_1_p7, busdisplay_1_p10, busdisplay_2_d1,
       busdisplay_2_d2, busdisplay_2_d3, busdisplay_2_d4, busdisplay_2_d5, busdisplay_3_p2, busdisplay_3_p5,
       busdisplay_3_p8, busdisplay_3_p11, busdisplay_3_p14, busdisplay_4_d1, busdisplay_4_d2,
       busdisplay_4_d3, busdisplay_4_d4, busdisplay_4_d5, rddisplay_2_p3;
  wire [9:0] rj32_1_p1;
  wire [15:0] aluopdisplay_1_d1, aluopdisplay_1_d2, instrdisplay_1_p2, instrdisplay_1_p4, instrdisplay_1_p6,
       instrdisplay_1_p8, instrdisplay_1_p10, instrdisplay_1_p12, Program_d, rddisplay_1_p2, rddisplay_1_p4,
       rddisplay_1_p7, rddisplay_2_p4, rddisplay_2_p8, rddisplay_2_p11, rddisplay_3_p2, rddisplay_3_p4,
       rddisplay_3_p7, rj32_1_p7, rj32_1_p9, rj32_1_p11;
  wire [33:0] busdisplay_2_o, busdisplay_3_p7, rddisplay_2_p7;
  wire [63:0] bus;

  BlockRAMDualPort #(.AddrBits(10), .isProgramMemory("true"), .Bits(16)) Program (
    .A(rj32_1_p1), .Din({16{1'b0}}), .str(1'b0), .C(MC), .D(Program_d));
  Button step (.out(step_t));
  Button slow (.out(slow_t));
  Button run (.out(run_t));
  LED stalled (.in(stalled_t));
  // rj32 rj32_1: pin names not known; wires that end beside it: rj32_1_p1, Program_d, MC, erun, rj32_1_p5, 1'b1, rj32_1_p7, run_t, rj32_1_p9, slow_t, rj32_1_p11, step_t, rj32_1_p13, clock, rj32_1_p15, \reg , stalled_t, skip, halt
  datamemio datamemio_1 (
    .we(rj32_1_p5), .D_in(rj32_1_p7), .A(rj32_1_p9), .D_out(rj32_1_p11), .req(rj32_1_p13), .ack(rj32_1_p15),
    .clk(clock));
  SixteenSeg sixteenseg_1 (.led(rddisplay_1_p2), .dp(rddisplay_1_p3));
  // rddisplay rddisplay_1: pin names not known; wires that end beside it: ctrl, rddisplay_1_p2, rddisplay_1_p3, rddisplay_1_p4, 1'b0, rddisplay_1_p6, rddisplay_1_p7, rddisplay_1_p8, rddisplay_1_p9
  SixteenSeg sixteenseg_2 (.led(instrdisplay_1_p2), .dp(instrdisplay_1_p3));
  SixteenSeg sixteenseg_3 (.led(instrdisplay_1_p4), .dp(instrdisplay_1_p5));
  // instrdisplay instrdisplay_1: pin names not known; wires that end beside it: ctrl, instrdisplay_1_p2, instrdisplay_1_p3, instrdisplay_1_p4, instrdisplay_1_p5, instrdisplay_1_p6, instrdisplay_1_p7, instrdisplay_1_p8, instrdisplay_1_p9, instrdisplay_1_p10, instrdisplay_1_p11, instrdisplay_1_p12, instrdisplay_1_p13
  SixteenSeg sixteenseg_4 (.led(rddisplay_1_p4), .dp(rddisplay_1_p6));
  SixteenSeg sixteenseg_5 (.led(rddisplay_1_p7), .dp(rddisplay_1_p8));
  SixteenSeg sixteenseg_6 (.led(instrdisplay_1_p6), .dp(instrdisplay_1_p7));
  SixteenSeg sixteenseg_7 (.led(instrdisplay_1_p8), .dp(instrdisplay_1_p9));
  Seven_Seg_Hex seven_seg_hex_1 (.d(busdisplay_1_p2), .dp(busdisplay_1_p3));
  // busdisplay busdisplay_1: pin names not known; wires that end beside it: rddisplay_1_p9, busdisplay_1_p2, busdisplay_1_p3, bus, busdisplay_1_p5, busdisplay_1_p6, busdisplay_1_p7, 2'b11, busdisplay_1_p9, busdisplay_1_p10, busdisplay_1_p11, hex
  SixteenSeg sixteenseg_8 (.led(instrdisplay_1_p10), .dp(instrdisplay_1_p11));
  SixteenSeg sixteenseg_9 (.led(instrdisplay_1_p12), .dp(instrdisplay_1_p13));
  Seven_Seg_Hex seven_seg_hex_2 (.d(busdisplay_1_p5), .dp(busdisplay_1_p6));
  Seven_Seg_Hex seven_seg_hex_3 (.d(busdisplay_1_p7), .dp(busdisplay_1_p9));
  SixteenSeg sixteenseg_10 (.led(rddisplay_2_p4), .dp(rddisplay_2_p6));
  DipSwitch u_hex (.out(hex));
  Seven_Seg_Hex seven_seg_hex_4 (.d(busdisplay_1_p10), .dp(busdisplay_1_p11));
  Seven_Seg_Hex seven_seg_hex_5 (.d(rddisplay_2_p3), .dp(rddisplay_2_p5));
  SixteenSeg sixteenseg_11 (.led(rddisplay_2_p8), .dp(rddisplay_2_p10));
  SixteenSeg sixteenseg_12 (.led(rddisplay_2_p11), .dp(rddisplay_2_p12));
  // rddisplay rddisplay_2: pin names not known; wires that end beside it: rddisplay_2_p1, rddisplay_2_p1, rddisplay_2_p3, rddisplay_2_p4, rddisplay_2_p5, rddisplay_2_p6, rddisplay_2_p7, rddisplay_2_p8, 1'b1, rddisplay_2_p10, rddisplay_2_p11, rddisplay_2_p12, rddisplay_2_p13
  Seven_Seg_Hex seven_seg_hex_6 (.d(busdisplay_2_d1), .dp(busdisplay_2_p1));
  busdisplay busdisplay_2 (
    .D1(busdisplay_2_d1), .P1(busdisplay_2_p1), .D2(busdisplay_2_d2), .P2(busdisplay_2_p2),
    .D3(busdisplay_2_d3), .P3(busdisplay_2_p3), .D4(busdisplay_2_d4), .P4(busdisplay_2_p4),
    .D5(busdisplay_2_d5), .P5(busdisplay_2_p5), .i(rddisplay_2_p7), .o(busdisplay_2_o), .B(bus), .S(2'b01),
    .H(hex));
  SixteenSeg sixteenseg_13 (.led(rddisplay_3_p2), .dp(rddisplay_3_p3));
  Seven_Seg_Hex seven_seg_hex_7 (.d(busdisplay_2_d2), .dp(busdisplay_2_p2));
  Seven_Seg_Hex seven_seg_hex_8 (.d(busdisplay_2_d3), .dp(busdisplay_2_p3));
  // debugreg debugreg_1: pin names not known; wires that end beside it: 5'b10001, \reg , debugreg_1_p3, PC
  // debugreg debugreg_2: pin names not known; wires that end beside it: {5{1'b0}}, debugreg_1_p3, debugreg_2_p3, RA
  // debugreg debugreg_3: pin names not known; wires that end beside it: error, db, 5'b01101, debugreg_2_p3, debugreg_3_p5, FP
  // debugreg debugreg_4: pin names not known; wires that end beside it: bus, ctrl, 5'b01110, debugreg_3_p5, debugreg_4_p5, BP
  // debugreg debugreg_5: pin names not known; wires that end beside it: 5'b01111, debugreg_4_p5, SP
  SixteenSeg sixteenseg_14 (.led(rddisplay_3_p4), .dp(rddisplay_3_p6));
  SixteenSeg sixteenseg_15 (.led(rddisplay_3_p7), .dp(rddisplay_3_p8));
  // rddisplay rddisplay_3: pin names not known; wires that end beside it: rddisplay_2_p13, rddisplay_3_p2, rddisplay_3_p3, rddisplay_3_p4, 1'b0, rddisplay_3_p6, rddisplay_3_p7, rddisplay_3_p8, rddisplay_3_p9, busdisplay_2_o
  Seven_Seg_Hex seven_seg_hex_9 (.d(busdisplay_2_d4), .dp(busdisplay_2_p4));
  Seven_Seg_Hex seven_seg_hex_10 (.d(busdisplay_2_d5), .dp(busdisplay_2_p5));
  Seven_Seg_Hex seven_seg_hex_11 (.d(busdisplay_3_p2), .dp(busdisplay_3_p3));
  SixteenSeg sixteenseg_16 (.led(aluopdisplay_1_d1), .dp(aluopdisplay_1_p1));
  aluopdisplay aluopdisplay_1 (
    .D1(aluopdisplay_1_d1), .P1(aluopdisplay_1_p1), .D2(aluopdisplay_1_d2), .P2(aluopdisplay_1_p2));  // open: I, Q, R, L
  // debugreg debugreg_6: pin names not known; wires that end beside it: 5'b00001, \reg , debugreg_6_p3, R1_a0
  // debugreg debugreg_7: pin names not known; wires that end beside it: 5'b00010, debugreg_6_p3, debugreg_7_p3, R2_a1
  // debugreg debugreg_8: pin names not known; wires that end beside it: 5'b00011, debugreg_7_p3, debugreg_8_p3, R3_a2
  // debugreg debugreg_9: pin names not known; wires that end beside it: 5'b00100, debugreg_8_p3, debugreg_9_p3, R4_s0
  // debugreg debugreg_10: pin names not known; wires that end beside it: 5'b00101, debugreg_9_p3, debugreg_10_p3, R5_s1
  Seven_Seg_Hex seven_seg_hex_12 (.d(busdisplay_3_p5), .dp(busdisplay_3_p6));
  Seven_Seg_Hex seven_seg_hex_13 (.d(busdisplay_3_p8), .dp(busdisplay_3_p10));
  // debugreg debugreg_11: pin names not known; wires that end beside it: 5'b00110, debugreg_10_p3, R6_s2
  // busdisplay busdisplay_3: pin names not known; wires that end beside it: rddisplay_3_p9, busdisplay_3_p2, busdisplay_3_p3, bus, busdisplay_3_p5, busdisplay_3_p6, busdisplay_3_p7, busdisplay_3_p8, 2'b00, busdisplay_3_p10, busdisplay_3_p11, busdisplay_3_p12, hex, busdisplay_3_p14, busdisplay_3_p15
  SixteenSeg sixteenseg_17 (.led(aluopdisplay_1_d2), .dp(aluopdisplay_1_p2));
  Seven_Seg_Hex seven_seg_hex_14 (.d(busdisplay_3_p11), .dp(busdisplay_3_p12));
  Seven_Seg_Hex seven_seg_hex_15 (.d(busdisplay_3_p14), .dp(busdisplay_3_p15));
  Seven_Seg_Hex seven_seg_hex_16 (.d(busdisplay_4_d1), .dp(busdisplay_4_p1));
  Seven_Seg_Hex seven_seg_hex_17 (.d(busdisplay_4_d2), .dp(busdisplay_4_p2));
  busdisplay busdisplay_4 (
    .D1(busdisplay_4_d1), .P1(busdisplay_4_p1), .D2(busdisplay_4_d2), .P2(busdisplay_4_p2),
    .D3(busdisplay_4_d3), .P3(busdisplay_4_p3), .D4(busdisplay_4_d4), .P4(busdisplay_4_p4),
    .D5(busdisplay_4_d5), .P5(busdisplay_4_p5), .i(busdisplay_3_p7), .B(bus), .S(2'b10), .H(hex));  // open: o
  Seven_Seg_Hex seven_seg_hex_18 (.d(busdisplay_4_d3), .dp(busdisplay_4_p3));
  Seven_Seg_Hex seven_seg_hex_19 (.d(busdisplay_4_d4), .dp(busdisplay_4_p4));
  Seven_Seg_Hex seven_seg_hex_20 (.d(busdisplay_4_d5), .dp(busdisplay_4_p5));
  // debugreg debugreg_12: pin names not known; wires that end beside it: 5'b00111, \reg , debugreg_12_p3, R7_s3
  // debugreg debugreg_13: pin names not known; wires that end beside it: 5'b01000, debugreg_12_p3, debugreg_13_p3, R8_t0
  // debugreg debugreg_14: pin names not known; wires that end beside it: 5'b01001, debugreg_13_p3, debugreg_14_p3, R9_t1
  // debugreg debugreg_15: pin names not known; wires that end beside it: 5'b01010, debugreg_14_p3, debugreg_15_p3, R10_t2
  // debugreg debugreg_16: pin names not known; wires that end beside it: 5'b01011, debugreg_15_p3, debugreg_16_p3, R11_t3
  // debugreg debugreg_17: pin names not known; wires that end beside it: 5'b01100, debugreg_16_p3, R12_t4
  LED u_skip (.in(skip));

  // Other names for the same wires on the sheet: C = clock

  // Notes on the sheet:
  //   clock: Hz: 100
  //   rj45 Creates
  //   =
endmodule
