// Digital circuit hexdisplay.dig as structural Verilog
module hexdisplay (
  input  E,
  input  [15:0] V,
  input  H,
  output [3:0] D1,
  output P1,
  output [3:0] D2,
  output P2,
  output [3:0] D3,
  output P3,
  output [3:0] D4,
  output P4,
  output [3:0] D5,
  output P5
);

  wire and_1_out, and_2_out, and_3_out, and_4_out, comparator_1_gt, comparator_2_gt, comparator_3_gt,
       comparator_4_gt, or_1_out, or_2_out, or_3_out, or_4_out;
  wire [2:0] priorityencoder_1_num;
  wire [3:0] multiplexer_1_out, multiplexer_1_out_2;
  wire [19:0] bin2bcd_1_o;
  wire [19:8] multiplexer_1_out_3;

  Comparator #(.Bits(3)) comparator_1 (.a(priorityencoder_1_num), .b(3'b011), .gt(comparator_1_gt));  // open: eq, lt
  and and_1 (and_1_out, comparator_1_gt, E);
  assign D1 = and_1_out ? multiplexer_1_out_3[19:16] : 4'bz;  // Driver driver_1
  or or_1 (or_1_out, multiplexer_1_out_3[16], multiplexer_1_out_3[17], multiplexer_1_out_3[18], multiplexer_1_out_3[19]);
  Comparator #(.Bits(3)) comparator_2 (.a(priorityencoder_1_num), .b(3'b010), .gt(comparator_2_gt));  // open: eq, lt
  and and_2 (and_2_out, comparator_2_gt, E);
  assign D2 = and_2_out ? multiplexer_1_out_3[15:12] : 4'bz;  // Driver driver_2
  or or_2 (or_2_out, multiplexer_1_out_3[12], multiplexer_1_out_3[13], multiplexer_1_out_3[14], multiplexer_1_out_3[15]);
  Comparator #(.Bits(3)) comparator_3 (.a(priorityencoder_1_num), .b(3'b001), .gt(comparator_3_gt));  // open: eq, lt
  and and_3 (and_3_out, comparator_3_gt, E);
  assign D3 = and_3_out ? multiplexer_1_out_3[11:8] : 4'bz;  // Driver driver_3
  or or_3 (or_3_out, multiplexer_1_out_3[8], multiplexer_1_out_3[9], multiplexer_1_out_3[10], multiplexer_1_out_3[11]);
  Comparator #(.Bits(3)) comparator_4 (.a(priorityencoder_1_num), .b(3'b000), .gt(comparator_4_gt));  // open: eq, lt
  and and_4 (and_4_out, comparator_4_gt, E);
  assign D4 = and_4_out ? multiplexer_1_out_2 : 4'bz;  // Driver driver_4
  or or_4 (or_4_out, multiplexer_1_out_2[0], multiplexer_1_out_2[1], multiplexer_1_out_2[2], multiplexer_1_out_2[3]);
  assign D5 = E ? multiplexer_1_out : 4'bz;  // Driver driver_5
  bin2bcd bin2bcd_1 (.I(V), .O(bin2bcd_1_o));
  PriorityEncoder #(.Selector_Bits(3)) priorityencoder_1 (
    .in0(1'b0), .in1(or_4_out), .in2(or_3_out), .in3(or_2_out), .in4(or_1_out), .in5(1'b0), .in6(1'b0),
    .in7(1'b0), .num(priorityencoder_1_num));  // open: any
  Multiplexer #(.Bits(20)) multiplexer_1 (
    .sel(H), .in_0(bin2bcd_1_o), .in_1({4'b0000, V}),
    .out({multiplexer_1_out_3, multiplexer_1_out_2, multiplexer_1_out}));

  assign P1 = 1'b0;
  assign P2 = 1'b0;
  assign P3 = 1'b0;
  assign P4 = 1'b0;
  assign P5 = 1'b0;
endmodule
