// Digital circuit instdecoder.dig as structural Verilog
module instdecoder (
  input  [1:0] fmt,
  input  [4:0] op0,
  output [4:0] op,
  output rd_valid,
  output rs_valid,
  output imm_valid,
  output mem,
  output i11,
  output imm_op
);

  wire decoder_1_out_1, ri6, ri8, rr;
  wire [4:0] multiplexer_1_out;

  Decoder #(.Selector_Bits(2)) decoder_1 (.sel(fmt), .out_0(rr), .out_1(decoder_1_out_1), .out_2(mem), .out_3(ri6));
  Demultiplexer demultiplexer_1 (.sel(op0[0]), .in(decoder_1_out_1), .out_0(ri8), .out_1(i11));
  Multiplexer #(.Bits(5)) multiplexer_1 (
    .sel(op0[0]), .in_0({4'b0011, op0[1]}), .in_1({3'b010, op0[2:1]}), .out(multiplexer_1_out));
  Multiplexer #(.Selector_Bits(2), .Bits(5)) multiplexer_2 (
    .sel(fmt), .in_0(op0), .in_1(multiplexer_1_out), .in_2({3'b011, op0[1:0]}), .in_3({1'b1, op0[3:0]}),
    .out(op));
  or or_1 (rs_valid, mem, rr);
  not not_1 (rd_valid, i11);
  nor nor_1 (imm_valid, rr, mem);
  and and_1 (imm_op, i11, op[0]);

  // Other names for the same wires on the sheet: ls = mem
endmodule
