// Digital circuit instrdisplay.dig as structural Verilog
module instrdisplay (
  input  [4:0] I,
  input  [2:0] C,
  output [15:0] D1,
  output P1,
  output [15:0] D2,
  output P2,
  output [15:0] D3,
  output P3,
  output [15:0] D4,
  output P4,
  output [15:0] D5,
  output P5,
  output [15:0] D6,
  output P6
);

  wire and_1_out;
  wire [6:0] multiplexer_1_out, multiplexer_2_out, multiplexer_3_out, multiplexer_4_out, multiplexer_5_out,
       multiplexer_6_out, multiplexer_7_out, multiplexer_8_out, multiplexer_9_out, multiplexer_10_out;

  Multiplexer #(.Selector_Bits(5), .Bits(7)) multiplexer_1 (
    .sel(I), .in_0(7'b0100000), .in_1(7'b0100000), .in_2(7'b0100000), .in_3(7'b0100000), .in_4(7'b0100000),
    .in_5(7'b0100000), .in_6(7'b0100000), .in_7(7'b0100000), .in_8(7'b0100000), .in_9(7'b0100000),
    .in_10(7'b0100000), .in_11(7'b0100000), .in_12(7'b0100000), .in_13(7'b0100000), .in_14(7'b0100000),
    .in_15(7'b0100000), .in_16(7'b0100000), .in_17(7'b0100000), .in_18(7'b0100000), .in_19(7'b0100000),
    .in_20(7'b0100000), .in_21(7'b0100000), .in_22(7'b0100000), .in_23(7'b0100000), .in_24(7'b0100000),
    .in_25(7'b1001001), .in_26(7'b0100000), .in_27(7'b0100000), .in_28(7'b0100000), .in_29(7'b0100000),
    .in_30(7'b0100000), .in_31(7'b0100000), .out(multiplexer_1_out));
  ROM #(.AddrBits(7), .Bits(16)) ASCII (.A(multiplexer_1_out), .sel(1'b1), .D(D1));
  Multiplexer #(.Selector_Bits(5), .Bits(7)) multiplexer_2 (
    .sel(I), .in_0(7'b0100000), .in_1(7'b0100000), .in_2(7'b1000101), .in_3(7'b0100000), .in_4(7'b0100000),
    .in_5(7'b0100000), .in_6(7'b0100000), .in_7(7'b0100000), .in_8(7'b0100000), .in_9(7'b0100000),
    .in_10(7'b0100000), .in_11(7'b0100000), .in_12(7'b0100000), .in_13(7'b0100000), .in_14(7'b0100000),
    .in_15(7'b0100000), .in_16(7'b0100000), .in_17(7'b0100000), .in_18(7'b0100000), .in_19(7'b0100000),
    .in_20(7'b0100000), .in_21(7'b0100000), .in_22(7'b0100000), .in_23(7'b0100000), .in_24(7'b1001001),
    .in_25(7'b1000110), .in_26(7'b0100000), .in_27(7'b0100000), .in_28(7'b0100000), .in_29(7'b0100000),
    .in_30(7'b0100000), .in_31(7'b1010011), .out(multiplexer_2_out));
  ROM #(.AddrBits(7), .Bits(16)) ASCII_2 (.A(multiplexer_2_out), .sel(1'b1), .D(D2));
  Multiplexer #(.Selector_Bits(5), .Bits(7)) multiplexer_3 (
    .sel(I), .in_0(7'b0100000), .in_1(7'b0100000), .in_2(7'b1010010), .in_3(7'b1001000), .in_4(7'b0100000),
    .in_5(7'b0100000), .in_6(7'b0100000), .in_7(7'b0100000), .in_8(7'b0100000), .in_9(7'b0100000),
    .in_10(7'b0100000), .in_11(7'b0100000), .in_12(7'b0100000), .in_13(7'b0100000), .in_14(7'b0100000),
    .in_15(7'b0100000), .in_16(7'b0100000), .in_17(7'b0100000), .in_18(7'b0100000), .in_19(7'b0100000),
    .in_20(7'b0100000), .in_21(7'b0100000), .in_22(7'b1001101), .in_23(7'b0100000), .in_24(7'b1000110),
    .in_25(7'b1000011), .in_26(7'b0100000), .in_27(7'b0100000), .in_28(7'b1001010), .in_29(7'b0100000),
    .in_30(7'b1001100), .in_31(7'b1010100), .out(multiplexer_3_out));
  ROM #(.AddrBits(7), .Bits(16)) ASCII_3 (.A(multiplexer_3_out), .sel(1'b1), .D(D3));
  Multiplexer #(.Selector_Bits(5), .Bits(7)) multiplexer_4 (
    .sel(I), .in_0(7'b1001110), .in_1(7'b0100000), .in_2(7'b1010010), .in_3(7'b1000001), .in_4(7'b0100000),
    .in_5(7'b0100000), .in_6(7'b0100000), .in_7(7'b0100000), .in_8(7'b0100000), .in_9(7'b0100000),
    .in_10(7'b0100000), .in_11(7'b0100000), .in_12(7'b0100000), .in_13(7'b0100000), .in_14(7'b0100000),
    .in_15(7'b0100000), .in_16(7'b1000001), .in_17(7'b0100000), .in_18(7'b0100000), .in_19(7'b0100000),
    .in_20(7'b0100000), .in_21(7'b0100000), .in_22(7'b1001111), .in_23(7'b0100000), .in_24(7'b0100000),
    .in_25(7'b0100000), .in_26(7'b1000010), .in_27(7'b1000010), .in_28(7'b1010101), .in_29(7'b0100000),
    .in_30(7'b1001111), .in_31(7'b1001111), .out(multiplexer_4_out));
  ROM #(.AddrBits(7), .Bits(16)) ASCII_4 (.A(multiplexer_4_out), .sel(1'b1), .D(D4));
  Multiplexer #(.Selector_Bits(5), .Bits(7)) multiplexer_5 (
    .sel(I), .in_0(7'b1001111), .in_1(7'b0100000), .in_2(7'b1001111), .in_3(7'b1001100), .in_4(7'b0100000),
    .in_5(7'b0100000), .in_6(7'b0100000), .in_7(7'b0100000), .in_8(7'b0100000), .in_9(7'b0100000),
    .in_10(7'b0100000), .in_11(7'b0100000), .in_12(7'b0100000), .in_13(7'b0100000), .in_14(7'b0100000),
    .in_15(7'b0100000), .in_16(7'b1000100), .in_17(7'b0100000), .in_18(7'b0100000), .in_19(7'b0100000),
    .in_20(7'b1000101), .in_21(7'b0100000), .in_22(7'b1010110), .in_23(7'b0100000), .in_24(7'b0100000),
    .in_25(7'b0100000), .in_26(7'b1010010), .in_27(7'b1010010), .in_28(7'b1001101), .in_29(7'b0100000),
    .in_30(7'b1000001), .in_31(7'b1010010), .out(multiplexer_5_out));
  Multiplexer #(.Selector_Bits(3), .Bits(7)) multiplexer_6 (
    .sel(C), .in_0(7'b0100000), .in_1(7'b1000101), .in_2(7'b1001110), .in_3(7'b1001100), .in_4(7'b1000111),
    .in_5(7'b1001100), .in_6(7'b1001000), .in_7(7'b0100000), .out(multiplexer_6_out));
  Multiplexer #(.Bits(7)) multiplexer_7 (
    .sel(and_1_out), .in_0(multiplexer_5_out), .in_1(multiplexer_6_out), .out(multiplexer_7_out));
  ROM #(.AddrBits(7), .Bits(16)) ASCII_5 (.A(multiplexer_7_out), .sel(1'b1), .D(D5));
  Multiplexer #(.Selector_Bits(5), .Bits(7)) multiplexer_8 (
    .sel(I), .in_0(7'b1010000), .in_1(7'b0100000), .in_2(7'b1010010), .in_3(7'b1010100), .in_4(7'b0100000),
    .in_5(7'b0100000), .in_6(7'b0100000), .in_7(7'b0100000), .in_8(7'b0100000), .in_9(7'b0100000),
    .in_10(7'b0100000), .in_11(7'b0100000), .in_12(7'b0100000), .in_13(7'b0100000), .in_14(7'b0100000),
    .in_15(7'b0100000), .in_16(7'b1000100), .in_17(7'b0100000), .in_18(7'b0100000), .in_19(7'b0100000),
    .in_20(7'b1010001), .in_21(7'b0100000), .in_22(7'b1000101), .in_23(7'b0100000), .in_24(7'b0100000),
    .in_25(7'b0100000), .in_26(7'b1010100), .in_27(7'b1000110), .in_28(7'b1010000), .in_29(7'b0100000),
    .in_30(7'b1000100), .in_31(7'b1000101), .out(multiplexer_8_out));
  Multiplexer #(.Selector_Bits(3), .Bits(7)) multiplexer_9 (
    .sel(C), .in_0(7'b0100000), .in_1(7'b1010001), .in_2(7'b1000101), .in_3(7'b1010100), .in_4(7'b1000101),
    .in_5(7'b1001111), .in_6(7'b1010011), .in_7(7'b0100000), .out(multiplexer_9_out));
  Multiplexer #(.Bits(7)) multiplexer_10 (
    .sel(and_1_out), .in_0(multiplexer_8_out), .in_1(multiplexer_9_out), .out(multiplexer_10_out));
  ROM #(.AddrBits(7), .Bits(16)) ASCII_6 (.A(multiplexer_10_out), .sel(1'b1), .D(D6));
  and and_1 (and_1_out, ~I[1], ~I[2], I[3], I[4]);  // And

  assign P1 = 1'b0;
  assign P2 = 1'b0;
  assign P3 = 1'b0;
  assign P4 = 1'b0;
  assign P5 = 1'b0;
  assign P6 = 1'b0;

  // Notes on the sheet:
  //   contents of ASCII (hex, n*v repeats v):
  //   90ff,c,377,33f,38c,3bb,3fb,f,3ff,3bf,3cf,4a3f,f3,483f,3f3,1c3,0,0,0,0,0,0,0,0,0,0,
  //   0,0,0,0,0,0,0,0,0,0,0,0,0,0,0,0,0,0,0,0,0,0,90ff,c,377,33f,38c,3bb,3fb,f,3ff,3bf,
  //   0,0,0,0,0,0,0,3cf,4a3f,f3,483f,3f3,1c3,2fb,3cc,4833,7c,31c0,f0,14cc,24cc,ff,3c7,20ff,
  //   23c7,3bb,4803,fc,90c0,a0cc,b400,5400,9033
  //   contents of ASCII_2 (hex, n*v repeats v):
  //   90ff,c,377,33f,38c,3bb,3fb,f,3ff,3bf,3cf,4a3f,f3,483f,3f3,1c3,0,0,0,0,0,0,0,0,0,0,
  //   0,0,0,0,0,0,0,0,0,0,0,0,0,0,0,0,0,0,0,0,0,0,90ff,c,377,33f,38c,3bb,3fb,f,3ff,3bf,
  //   0,0,0,0,0,0,0,3cf,4a3f,f3,483f,3f3,1c3,2fb,3cc,4833,7c,31c0,f0,14cc,24cc,ff,3c7,20ff,
  //   23c7,3bb,4803,fc,90c0,a0cc,b400,5400,9033
  //   contents of ASCII_3 (hex, n*v repeats v):
  //   90ff,c,377,33f,38c,3bb,3fb,f,3ff,3bf,3cf,4a3f,f3,483f,3f3,1c3,0,0,0,0,0,0,0,0,0,0,
  //   0,0,0,0,0,0,0,0,0,0,0,0,0,0,0,0,0,0,0,0,0,0,90ff,c,377,33f,38c,3bb,3fb,f,3ff,3bf,
  //   0,0,0,0,0,0,0,3cf,4a3f,f3,483f,3f3,1c3,2fb,3cc,4833,7c,31c0,f0,14cc,24cc,ff,3c7,20ff,
  //   23c7,3bb,4803,fc,90c0,a0cc,b400,5400,9033
  //   contents of ASCII_4 (hex, n*v repeats v):
  //   90ff,c,377,33f,38c,3bb,3fb,f,3ff,3bf,3cf,4a3f,f3,483f,3f3,1c3,0,0,0,0,0,0,0,0,0,0,
  //   0,0,0,0,0,0,0,0,0,0,0,0,0,0,0,0,0,0,0,0,0,0,90ff,c,377,33f,38c,3bb,3fb,f,3ff,3bf,
  //   0,0,0,0,0,0,0,3cf,4a3f,f3,483f,3f3,1c3,2fb,3cc,4833,7c,31c0,f0,14cc,24cc,ff,3c7,20ff,
  //   23c7,3bb,4803,fc,90c0,a0cc,b400,5400,9033
  //   contents of ASCII_5 (hex, n*v repeats v):
  //   90ff,c,377,33f,38c,3bb,3fb,f,3ff,3bf,3cf,4a3f,f3,483f,3f3,1c3,0,0,0,0,0,0,0,0,0,0,
  //   0,0,0,0,0,0,0,0,0,0,0,0,0,0,0,0,0,0,0,0,0,0,90ff,c,377,33f,38c,3bb,3fb,f,3ff,3bf,
  //   0,0,0,0,0,0,0,3cf,4a3f,f3,483f,3f3,1c3,2fb,3cc,4833,7c,31c0,f0,14cc,24cc,ff,3c7,20ff,
  //   23c7,3bb,4803,fc,90c0,a0cc,b400,5400,9033
  //   contents of ASCII_6 (hex, n*v repeats v):
  //   90ff,c,377,33f,38c,3bb,3fb,f,3ff,3bf,3cf,4a3f,f3,483f,3f3,1c3,0,0,0,0,0,0,0,0,0,0,
  //   0,0,0,0,0,0,0,0,0,0,0,0,0,0,0,0,0,0,0,0,0,0,90ff,c,377,33f,38c,3bb,3fb,f,3ff,3bf,
  //   0,0,0,0,0,0,0,3cf,4a3f,f3,483f,3f3,1c3,2fb,3cc,4833,7c,31c0,f0,14cc,24cc,ff,3c7,20ff,
  //   23c7,3bb,4803,fc,90c0,a0cc,b400,5400,9033
endmodule
