// Digital circuit memaccess.dig as structural Verilog
module memaccess (
  input  [15:0] result,
  input  [15:0] rdval,
  input  mem,
  input  [1:0] memop,
  input  [15:0] D,
  output [15:0] wrval,
  output [15:0] A,
  output [15:0] D_in,
  output str
);

  Multiplexer #(.Selector_Bits(2), .Bits(16)) multiplexer_1 (
    .sel({mem, memop[0]}), .in_0(result), .in_1(result), .in_2(D), .in_3(rdval), .out(wrval));
  and and_1 (str, memop[0], mem);

  assign A = result;
  assign D_in = rdval;
endmodule
