// Digital circuit num2ascii.dig as structural Verilog
module num2ascii (
  input  [15:0] num,
  input  [2:0] digit,
  input  \signed ,
  output [6:0] char
);

  wire and_1_out;
  wire [6:0] bcd2ascii_1_d0, bcd2ascii_1_d1, bcd2ascii_1_d2, bcd2ascii_1_d3, bcd2ascii_1_d4, bcd2ascii_1_d5;
  wire [15:0] multiplexer_1_out, neg_1_out;

  Neg #(.Bits(16)) neg_1 (.in(num), .out(neg_1_out));
  and and_1 (and_1_out, num[15], \signed );
  Multiplexer #(.Bits(16)) multiplexer_1 (.sel(and_1_out), .in_0(num), .in_1(neg_1_out), .out(multiplexer_1_out));
  bcd2ascii bcd2ascii_1 (
    .N({4'b0000, multiplexer_1_out}), .s(and_1_out), .d5(bcd2ascii_1_d5), .d4(bcd2ascii_1_d4),
    .d3(bcd2ascii_1_d3), .d2(bcd2ascii_1_d2), .d1(bcd2ascii_1_d1), .d0(bcd2ascii_1_d0));
  Multiplexer #(.Selector_Bits(3), .Bits(7)) multiplexer_2 (
    .sel(digit), .in_0(bcd2ascii_1_d5), .in_1(bcd2ascii_1_d4), .in_2(bcd2ascii_1_d3), .in_3(bcd2ascii_1_d2),
    .in_4(bcd2ascii_1_d1), .in_5(bcd2ascii_1_d0), .in_6({7{1'b0}}), .in_7({7{1'b0}}), .out(char));
endmodule
