// Digital circuit op2ascii.dig as structural Verilog
module op2ascii (
  input  [15:0] I,
  output [6:0] L0,
  output [6:0] L1,
  output [6:0] L2,
  output [6:0] L3,
  output [6:0] L4,
  output [6:0] L5
);

  Multiplexer #(.Selector_Bits(5), .Bits(7)) multiplexer_1 (
    .sel(I[4:0]), .in_0(7'b0100000), .in_1(7'b0100000), .in_2(7'b0100000), .in_3(7'b0100000),
    .in_4(7'b0100000), .in_5(7'b0100000), .in_6(7'b0100000), .in_7(7'b0100000), .in_8(7'b0100000),
    .in_9(7'b0100000), .in_10(7'b0100000), .in_11(7'b0100000), .in_12(7'b0100000), .in_13(7'b0100000),
    .in_14(7'b0100000), .in_15(7'b1010011), .in_16(7'b0100000), .in_17(7'b0100000), .in_18(7'b0100000),
    .in_19(7'b0100000), .in_20(7'b0100000), .in_21(7'b0100000), .in_22(7'b0100000), .in_23(7'b0100000),
    .in_24(7'b0100000), .in_25(7'b0100000), .in_26(7'b0100000), .in_27(7'b0100000), .in_28(7'b0100000),
    .in_29(7'b0100000), .in_30(7'b0100000), .in_31(7'b0100000), .out(L0));
  Multiplexer #(.Selector_Bits(5), .Bits(7)) multiplexer_2 (
    .sel(I[4:0]), .in_0(7'b0100000), .in_1(7'b0100000), .in_2(7'b1000101), .in_3(7'b0100000),
    .in_4(7'b0100000), .in_5(7'b0100000), .in_6(7'b0100000), .in_7(7'b0100000), .in_8(7'b0100000),
    .in_9(7'b0100000), .in_10(7'b0100000), .in_11(7'b0100000), .in_12(7'b0100000), .in_13(7'b1010011),
    .in_14(7'b1001100), .in_15(7'b1010100), .in_16(7'b0100000), .in_17(7'b0100000), .in_18(7'b0100000),
    .in_19(7'b0100000), .in_20(7'b0100000), .in_21(7'b0100000), .in_22(7'b0100000), .in_23(7'b0100000),
    .in_24(7'b0100000), .in_25(7'b0100000), .in_26(7'b1001001), .in_27(7'b1001001), .in_28(7'b1001001),
    .in_29(7'b1001001), .in_30(7'b1001001), .in_31(7'b1001001), .out(L1));
  Multiplexer #(.Selector_Bits(5), .Bits(7)) multiplexer_3 (
    .sel(I[4:0]), .in_0(7'b0100000), .in_1(7'b0100000), .in_2(7'b1010010), .in_3(7'b1001000),
    .in_4(7'b1001010), .in_5(7'b0100000), .in_6(7'b1001101), .in_7(7'b0100000), .in_8(7'b1001010),
    .in_9(7'b0100000), .in_10(7'b1000011), .in_11(7'b0100000), .in_12(7'b1001100), .in_13(7'b1010100),
    .in_14(7'b1001111), .in_15(7'b1001111), .in_16(7'b0100000), .in_17(7'b0100000), .in_18(7'b1000001),
    .in_19(7'b1010011), .in_20(7'b0100000), .in_21(7'b0100000), .in_22(7'b0100000), .in_23(7'b0100000),
    .in_24(7'b0100000), .in_25(7'b0100000), .in_26(7'b1000110), .in_27(7'b1000110), .in_28(7'b1000110),
    .in_29(7'b1000110), .in_30(7'b1000110), .in_31(7'b1000110), .out(L2));
  Multiplexer #(.Selector_Bits(5), .Bits(7)) multiplexer_4 (
    .sel(I[4:0]), .in_0(7'b1001110), .in_1(7'b0100000), .in_2(7'b1010010), .in_3(7'b1000001),
    .in_4(7'b1010101), .in_5(7'b0100000), .in_6(7'b1001111), .in_7(7'b0100000), .in_8(7'b1010101),
    .in_9(7'b1001001), .in_10(7'b1000001), .in_11(7'b1001001), .in_12(7'b1001111), .in_13(7'b1001111),
    .in_14(7'b1000001), .in_15(7'b1010010), .in_16(7'b1000001), .in_17(7'b1010011), .in_18(7'b1000100),
    .in_19(7'b1010101), .in_20(7'b1011000), .in_21(7'b1000001), .in_22(7'b0100000), .in_23(7'b1010011),
    .in_24(7'b1010011), .in_25(7'b1000001), .in_26(7'b0100000), .in_27(7'b0100000), .in_28(7'b0100000),
    .in_29(7'b0100000), .in_30(7'b0100000), .in_31(7'b0100000), .out(L3));
  Multiplexer #(.Selector_Bits(5), .Bits(7)) multiplexer_5 (
    .sel(I[4:0]), .in_0(7'b1001111), .in_1(7'b0100000), .in_2(7'b1001111), .in_3(7'b1001100),
    .in_4(7'b1001101), .in_5(7'b0100000), .in_6(7'b1010110), .in_7(7'b0100000), .in_8(7'b1001101),
    .in_9(7'b1001101), .in_10(7'b1001100), .in_11(7'b1001101), .in_12(7'b1000001), .in_13(7'b1010010),
    .in_14(7'b1000100), .in_15(7'b1000101), .in_16(7'b1000100), .in_17(7'b1010101), .in_18(7'b1000100),
    .in_19(7'b1000010), .in_20(7'b1001111), .in_21(7'b1001110), .in_22(7'b1001111), .in_23(7'b1001000),
    .in_24(7'b1001000), .in_25(7'b1010011), .in_26(7'b1000101), .in_27(7'b1001110), .in_28(7'b1001100),
    .in_29(7'b1000111), .in_30(7'b1001100), .in_31(7'b1001000), .out(L4));
  Multiplexer #(.Selector_Bits(5), .Bits(7)) multiplexer_6 (
    .sel(I[4:0]), .in_0(7'b1010000), .in_1(7'b0100000), .in_2(7'b1010010), .in_3(7'b1010100),
    .in_4(7'b1010000), .in_5(7'b0100000), .in_6(7'b1000101), .in_7(7'b0100000), .in_8(7'b1010000),
    .in_9(7'b1001101), .in_10(7'b1001100), .in_11(7'b1001101), .in_12(7'b1000100), .in_13(7'b1000101),
    .in_14(7'b1000010), .in_15(7'b1000010), .in_16(7'b1000100), .in_17(7'b1000010), .in_18(7'b1000011),
    .in_19(7'b1000011), .in_20(7'b1010010), .in_21(7'b1000100), .in_22(7'b1010010), .in_23(7'b1001100),
    .in_24(7'b1010010), .in_25(7'b1010010), .in_26(7'b1010001), .in_27(7'b1000101), .in_28(7'b1010100),
    .in_29(7'b1000101), .in_30(7'b1001111), .in_31(7'b1010011), .out(L5));
endmodule
