// Digital circuit rddisplay.dig as structural Verilog
module rddisplay (
  input  [33:0] i,
  input  C,
  output [15:0] D1,
  output P1,
  output [15:0] D2,
  output P2,
  output [33:0] o,
  output [15:0] D3,
  output P3
);

  wire decodedec_1_pc, decodedec_1_valid;
  wire [3:0] ctrlbreakout_1_p2, ctrlbreakout_1_p4, decodedec_1_r;
  wire [5:0] multiplexer_1_out;
  wire [5:4] ctrlbreakout_1_p5;
  wire [5:5] ctrlbreakout_1_p3;

  // ctrlbreakout ctrlbreakout_1: pin names not known; wires that end beside it: i, ctrlbreakout_1_p2, ctrlbreakout_1_p3[5], ctrlbreakout_1_p4, ctrlbreakout_1_p5[4], ctrlbreakout_1_p5[5]
  Multiplexer #(.Bits(6)) multiplexer_1 (
    .sel(C), .in_0({ctrlbreakout_1_p3[5], 1'b0, ctrlbreakout_1_p2}),
    .in_1({ctrlbreakout_1_p5, ctrlbreakout_1_p4}), .out(multiplexer_1_out));
  decodedec decodedec_1 (.D(multiplexer_1_out), .r(decodedec_1_r), .pc(decodedec_1_pc), .valid(decodedec_1_valid));
  regdisplay regdisplay_1 (
    .D1(D1), .P1(P1), .D2(D2), .P2(P2), .D3(D3), .P3(P3), .R(decodedec_1_r), .J(decodedec_1_pc),
    .E(decodedec_1_valid));

  assign o = i;
endmodule
