// Digital circuit regdisplay.dig as structural Verilog
module regdisplay (
  input  [3:0] R,
  input  E,
  input  J,
  output [15:0] D1,
  output P1,
  output [15:0] D2,
  output P2,
  output [15:0] D3,
  output P3
);

  wire [6:0] reg2ascii_1_d_0, reg2ascii_1_d_1, reg2ascii_1_d_2;

  reg2ascii reg2ascii_1 (.R(R), .J(J), .E(E), .D_0(reg2ascii_1_d_0), .D_1(reg2ascii_1_d_1), .D_2(reg2ascii_1_d_2));
  ROM #(.AddrBits(7), .Bits(16)) ASCII (.A(reg2ascii_1_d_0), .sel(1'b1), .D(D1));
  ROM #(.AddrBits(7), .Bits(16)) ASCII_2 (.A(reg2ascii_1_d_1), .sel(1'b1), .D(D2));
  ROM #(.AddrBits(7), .Bits(16)) ASCII_3 (.A(reg2ascii_1_d_2), .sel(1'b1), .D(D3));

  assign P1 = 1'b0;
  assign P2 = 1'b0;
  assign P3 = 1'b0;

  // Notes on the sheet:
  //   contents of ASCII (hex, n*v repeats v):
  //   90ff,c,377,33f,38c,3bb,3fb,f,3ff,3bf,3cf,4a3f,f3,483f,3f3,1c3,0,0,0,0,0,0,0,0,0,0,
  //   0,0,0,0,0,0,0,0,0,0,0,0,0,0,0,0,0,0,0,0,0,0,90ff,c,377,33f,38c,3bb,3fb,f,3ff,3bf,
  //   0,0,0,0,0,0,0,3cf,4a3f,f3,483f,3f3,1c3,2fb,3cc,4833,7c,31c0,f0,14cc,24cc,ff,3c7,20ff,
  //   23c7,3bb,4803,fc,90c0,a0cc,b400,5400,9033
  //   contents of ASCII_2 (hex, n*v repeats v):
  //   90ff,c,377,33f,38c,3bb,3fb,f,3ff,3bf,3cf,4a3f,f3,483f,3f3,1c3,0,0,0,0,0,0,0,0,0,0,
  //   0,0,0,0,0,0,0,0,0,0,0,0,0,0,0,0,0,0,0,0,0,0,90ff,c,377,33f,38c,3bb,3fb,f,3ff,3bf,
  //   0,0,0,0,0,0,0,3cf,4a3f,f3,483f,3f3,1c3,2fb,3cc,4833,7c,31c0,f0,14cc,24cc,ff,3c7,20ff,
  //   23c7,3bb,4803,fc,90c0,a0cc,b400,5400,9033
  //   contents of ASCII_3 (hex, n*v repeats v):
  //   90ff,c,377,33f,38c,3bb,3fb,f,3ff,3bf,3cf,4a3f,f3,483f,3f3,1c3,0,0,0,0,0,0,0,0,0,0,
  //   0,0,0,0,0,0,0,0,0,0,0,0,0,0,0,0,0,0,0,0,0,0,90ff,c,377,33f,38c,3bb,3fb,f,3ff,3bf,
  //   0,0,0,0,0,0,0,3cf,4a3f,f3,483f,3f3,1c3,2fb,3cc,4833,7c,31c0,f0,14cc,24cc,ff,3c7,20ff,
  //   23c7,3bb,4803,fc,90c0,a0cc,b400,5400,9033
endmodule
