// Digital circuit regfile.dig as structural Verilog
module regfile (
  input  [1:0] rs,
  input  [1:0] rd,
  input  [31:0] result,
  input  clock,
  output [31:0] rdval,
  output [31:0] rsval,
  output [31:0] R0,
  output [31:0] R1,
  output [31:0] R2,
  output [31:0] R3
);

  wire decoder_1_out_0, decoder_1_out_1, decoder_1_out_2, decoder_1_out_3;
  wire [31:0] demultiplexer_1_out_0, demultiplexer_1_out_1, demultiplexer_1_out_2, demultiplexer_1_out_3;

  Demultiplexer #(.Selector_Bits(2), .Bits(32)) demultiplexer_1 (
    .sel(rd), .in(result), .out_0(demultiplexer_1_out_0), .out_1(demultiplexer_1_out_1),
    .out_2(demultiplexer_1_out_2), .out_3(demultiplexer_1_out_3));
  Decoder #(.Selector_Bits(2)) decoder_1 (
    .sel(rd), .out_0(decoder_1_out_0), .out_1(decoder_1_out_1), .out_2(decoder_1_out_2),
    .out_3(decoder_1_out_3));
  Register #(.Bits(32)) u_R0 (.D(demultiplexer_1_out_0), .C(clock), .en(decoder_1_out_0), .Q(R0));
  Register #(.Bits(32)) u_R1 (.D(demultiplexer_1_out_1), .C(clock), .en(decoder_1_out_1), .Q(R1));
  Register #(.Bits(32)) u_R2 (.D(demultiplexer_1_out_2), .C(clock), .en(decoder_1_out_2), .Q(R2));
  Register #(.Bits(32)) u_R3 (.D(demultiplexer_1_out_3), .C(clock), .en(decoder_1_out_3), .Q(R3));
  Multiplexer #(.Selector_Bits(2), .Bits(32)) multiplexer_1 (
    .sel(rs), .in_0(R0), .in_1(R1), .in_2(R2), .in_3(R3), .out(rsval));
  Multiplexer #(.Selector_Bits(2), .Bits(32)) multiplexer_2 (
    .sel(rd), .in_0(R0), .in_1(R1), .in_2(R2), .in_3(R3), .out(rdval));
endmodule
