// Digital circuit rj32.dig as structural Verilog
module rj32 (
  input  clock,
  input  step,
  input  run_slow,
  input  [15:0] D_prog,
  input  [15:0] D_in,
  input  run_fast,
  input  run_faster,
  input  erun,
  input  ack,
  output halt,
  output error,
  output skip,
  output stall,
  output [9:0] A_prog,
  output clock_m,
  output [15:0] A_data,
  output [15:0] D_out,
  output w_en,
  output [25:0] db,
  output req,
  output [33:0] ctrl,
  output [63:0] bus,
  output [38:0] \reg 
);

  wire execute_1_p5, execute_1_p6, fetch_1_p7, skip_n, writeback_1_p8, writeback_1_p9;
  wire [15:0] decoder_1_p1, decoder_1_p2;

  not not_1 (clock_m, clock);
  // fetch fetch_1: pin names not known; wires that end beside it: bus[47:32], D_prog, clock, ctrl[11], ctrl[4], ctrl[12], fetch_1_p7, {\reg [37:32], A_prog}
  // decoder decoder_1: pin names not known; wires that end beside it: decoder_1_p1, decoder_1_p2, fetch_1_p7, {\reg [37:32], A_prog}, ctrl[4], clock, ctrl[11], ctrl[33:30], ctrl[28:25], bus[15:0], bus[31:16], ctrl[20:16], ctrl[29], ctrl[24], bus[63:48], ctrl[15]
  // clockctrl clockctrl_1: pin names not known; wires that end beside it: clock, step, run_slow, run_fast, run_faster, erun, ctrl[0]
  // control control_1: pin names not known; wires that end beside it: ctrl[20:16], ctrl[0], clock, skip_n, ack, ctrl[7:5], ctrl[23:21], ctrl[1], ctrl[2], ctrl[3], ctrl[12], ctrl[8], ctrl[9], ctrl[11], ctrl[4], ctrl[10], ctrl[14:13]
  // execute execute_1: pin names not known; wires that end beside it: bus[15:0], bus[31:16], ctrl[7:5], ctrl[23:21], execute_1_p5, execute_1_p6, bus[47:32], skip_n
  // writeback writeback_1: pin names not known; wires that end beside it: execute_1_p5, execute_1_p6, bus[47:32], decoder_1_p1, D_in, ctrl[14:13], \reg [15:0], writeback_1_p8, writeback_1_p9
  debugbus debugbus_1 (
    .db_ready(1'b1), .clock(clock), .ctrl(ctrl[15:0]), .wrval(\reg [15:0]), .result(bus[47:32]),
    .L(bus[15:0]), .R(bus[31:16]), .imm(bus[63:48]), .pc({\reg [37:32], A_prog}),
    .fullop({{8{1'b0}}, ctrl[23:16]}), .rdf({{10{1'b0}}, ctrl[24], ctrl[4], ctrl[28:25]}),
    .rsf({{10{1'b0}}, ctrl[29], 1'b0, ctrl[33:30]}), .db(db));
  // memaccess memaccess_1: pin names not known; wires that end beside it: writeback_1_p8, writeback_1_p9, ctrl[9], ctrl[12], ctrl[8], clock, A_data, w_en, D_out, req
  regfile regfile_1 (
    .rs(ctrl[33:30]), .rd(ctrl[28:25]), .result(\reg [15:0]), .clock(clock), .en(ctrl[12]), .wr(ctrl[10]),
    .rdval(decoder_1_p1), .rsval(decoder_1_p2));  // open: R0, R1, R2, R3

  assign error = ctrl[3];
  assign halt = ctrl[2];
  assign {\reg [38], \reg [31:16]} = {clock, A_prog, ctrl[10], ctrl[12], ctrl[28:25]};
  assign skip = ctrl[1];
  assign stall = ctrl[0];

  // Other names for the same wires on the sheet: A_data_t[15:0] = A_data; ack_t = ack; aluop_t[2:0] = ctrl[7:5];
  //   ctrl_t[15:0] = ctrl[15:0]; C = clock; cond_t[2:0] = ctrl[23:21]; fullop_t[7:0] = ctrl[23:16];
  //   D_in_t[15:0] = D_in; D_out_t[15:0] = D_out; D_prog_t[15:0] = D_prog; en = ctrl[12]; en_fetch = ctrl[11];
  //   error_t = ctrl[3]; halt_t = ctrl[2]; imm_t[15:0] = bus[63:48]; immv_t = ctrl[15]; jump_t = ctrl[4];
  //   rdf_t[5:0] = {ctrl[24], ctrl[4], ctrl[28:25]}; L_t[15:0] = bus[15:0]; mem_t = ctrl[8]; op_t[4:0] = ctrl[20:16];
  //   A_prog_t[15:0] = {\reg [37:32], A_prog}; PC_t[15:0] = {\reg [37:32], A_prog}; R_t[15:0] = bus[31:16];
  //   rd_t[3:0] = ctrl[28:25]; rdvalid_t = ctrl[24]; req_t = req; result_t[15:0] = bus[47:32];
  //   rs_t[3:0] = ctrl[33:30]; rsf_t (some bits) = {ctrl[29], ctrl[33:30]}; rsvalid_t = ctrl[29]; skip_t = ctrl[1];
  //   stall_t = ctrl[0]; store_t = ctrl[9]; W_en_t = w_en; write_t = ctrl[10]; wrmux_t[1:0] = ctrl[14:13];
  //   wrval_t[15:0] = \reg [15:0]

  // Notes on the sheet:
  //   clock: Hz: 10
  //   rj45 Creates
endmodule
