// Digital circuit rsdisplay.dig as structural Verilog
module rsdisplay (
  input  [25:0] i,
  output [15:0] D1,
  output P1,
  output [15:0] D2,
  output P2,
  output [25:0] o
);

  wire decodedec_1_valid;
  wire [1:0] ctrldec_1_p2;
  wire [15:0] debugval_1_q, debugval_2_q;
  wire [25:0] debugval_1_db_o;

  debugval debugval_1 (.db_i(i), .sel(8'h10), .db_o(debugval_1_db_o), .Q(debugval_1_q));
  decodedec decodedec_1 (.D(debugval_1_q), .valid(decodedec_1_valid));  // open: r, pc
  regdisplay regdisplay_1 (.D1(D1), .P1(P1), .D2(D2), .P2(P2), .E(decodedec_1_valid), .J(1'b0), .R(ctrldec_1_p2));
  debugval debugval_2 (.db_i(debugval_1_db_o), .sel(8'h11), .db_o(o), .Q(debugval_2_q));
  // ctrldec ctrldec_1: pin names not known; wires that end beside it: debugval_2_q, ctrldec_1_p2
endmodule
