// Digital circuit testsuite.dig as structural Verilog
module testsuite (
  input  clock,
  input  run,
  output error,
  output halt,
  output [15:0] PC
);

  frontpanel frontpanel_1 (
    .clock(clock), .erun(run), .DC(1'b0), .PC(PC), .halt(halt), .error(error));  // open: R0, R1, R2, R3
endmodule

/* Test case jump:
clock run error halt

# #include "../cpudef.asm"
# 
#   jump one
#   error
# three:
#   add r0, r1
#   add r0, r2
#   jump end
#   error
# two:
#   move r2, 2
#   jump three
#   error
# one:
#   move r1, 3
#   jump two
#   error
# end:
#   if.ne r0, 5
#   error
#   halt

program(0x010d, 0x0008, 0x0140, 0x0240, 0x00ed, 0x0008, 0x2021, 0xff4d, 0x0008, 0x1031, 0xff6d, 0x0008, 0x016f, 0x0008, 0x000c)

let i = 0;
while(!(halt | error | (i >= 100)))
  let i = i + 1;
  0 1 0 0
  1 1 x x
end while
0 1 0 1
*/

/* Test case if.eq:
clock run error halt

# #include "../cpudef.asm"
# 
# move r1, 2
# move r2, 3
# move r3, 3
# 
# ; skip r-r
# if.eq r1, r2
# error
# 
# ; skip r-i
# if.eq r1, 3
# error
# 
# ; no-skip r-r
# if.eq r2, r3
# jump p1
# error
# p1:
# 
# ; no-skip r-i
# if.eq r2, 3
# jump p2
# error
# p2:
# 
# halt

program(0x1021, 0x2031, 0x3031, 0x1268, 0x0008, 0x10eb, 0x0008, 0x2368, 0x002d, 0x0008, 0x20eb, 0x002d, 0x0008, 0x000c)

let i = 0;
while(!(halt | error | (i >= 100)))
  let i = i + 1;
  0 1 0 0
  1 1 x x
end while
0 1 0 1
*/

/* Test case if.lt:
clock run error halt

# #include "../cpudef.asm"
# 
# move r1, -1
# move r2, 0
# 
# ; skip r-r
# if.lt r2, r1
# error
# 
# ; skip r-r equal
# if.lt r2, r2
# error
# 
# ; skip r-i
# if.lt r2, -1
# error
# 
# ; skip r-i equal
# if.lt r2, 0
# error
# 
# ; no-skip r-r
# if.lt r1, r2
# jump p1
# error
# p1:
# 
# ; no-skip r-i
# if.lt r1, 1
# jump p2
# error
# p2:
# 
# halt

program(0x1ff1, 0x2001, 0x2170, 0x0008, 0x2270, 0x0008, 0x2ff3, 0x0008, 0x2033, 0x0008, 0x1270, 0x002d, 0x0008, 0x1073, 0x002d, 0x0008, 0x000c)

let i = 0;
while(!(halt | error | (i >= 100)))
  let i = i + 1;
  0 1 0 0
  1 1 x x
end while
0 1 0 1
*/

/* Test case if.lo:
clock run error halt

# #include "../cpudef.asm"
# 
# move r1, 0
# move r2, -1 ; 0xffff
# 
# ; skip r-r
# if.lo r2, r1
# error
# 
# ; skip r-r equal
# if.lo r2, r2
# error
# 
# ; skip r-i
# if.lo r2, 0
# error
# 
# ; skip r-i equal
# if.lo r2, -1
# error
# 
# ; no-skip r-r
# if.lo r1, r2
# jump p1
# error
# p1:
# 
# ; no-skip r-i
# if.lo r1, 1
# jump p2
# error
# p2:
# 
# halt

program(0x1001, 0x2ff1, 0x2178, 0x0008, 0x2278, 0x0008, 0x203b, 0x0008, 0x2ffb, 0x0008, 0x1278, 0x002d, 0x0008, 0x107b, 0x002d, 0x0008, 0x000c)

let i = 0;
while(!(halt | error | (i >= 100)))
  let i = i + 1;
  0 1 0 0
  1 1 x x
end while
0 1 0 1
*/

/* Test case loadstore:
clock run error halt

# #include "../cpudef.asm"
# 
# move r0, 2
# move r1, 5
# 
# ; memory doesn't have 5
# load r2, [r0,0]
# if.eq r2, 5
# error
# 
# ; store and check it does have 5
# store [r0,0], r1
# load r2, [r0,0]
# if.ne r2, 5
# error
# 
# ; check max offset of 15
# move r1, 7
# store [r0,15], r1
# load r2, [r0,15]
# if.ne r2, 7
# error
# 
# ; check base equivalent to offset
# move r2, 0
# add r0, 15
# load r2, [r0, 0]
# if.ne r2, 7
# error
# 
# ; check multiple writes and reads in a row
# move r1, 1
# move r2, 2
# move r3, 3
# move r4, 4
# move r5, 5
# move r6, 6
# move r0, 0
# store [r0, 3], r3
# store [r0, 1], r1
# store [r0, 6], r6
# store [r0, 2], r2
# store [r0, 4], r4
# store [r0, 5], r5
# move r1, -1
# move r2, -1
# move r3, -1
# move r4, -1
# move r5, -1
# move r6, -1
# load r5, [r0, 5]
# load r1, [r0, 1]
# load r6, [r0, 6]
# load r2, [r0, 2]
# load r4, [r0, 4]
# load r3, [r0, 3]
# if.ne r1, 1
#   error
# if.ne r2, 2
#   error
# if.ne r3, 3
#   error
# if.ne r4, 4
#   error
# if.ne r5, 5
#   error
# if.ne r6, 6
#   error
# 
# load r3, [r0, 3]
# jump skiperr1
# error
# skiperr1:
# 
# store [r0, 3], r3
# jump skiperr2
# error
# skiperr2:
# 
# halt

program(0x0021, 0x1051, 0x2002, 0x216b, 0x0008, 0x1006, 0x2002, 0x216f, 0x0008, 0x1071, 0x10f6, 0x20f2, 0x21ef, 0x0008, 0x2001, 0x03c3, 0x2002, 0x21ef, 0x0008, 0x1011, 0x2021, 0x3031, 0x4041, 0x5051, 0x6061, 0x0001, 0x3036, 0x1016, 0x6066, 0x2026, 0x4046, 0x5056, 0x1ff1, 0x2ff1, 0x3ff1, 0x4ff1, 0x5ff1, 0x6ff1, 0x5052, 0x1012, 0x6062, 0x2022, 0x4042, 0x3032, 0x106f, 0x0008, 0x20af, 0x0008, 0x30ef, 0x0008, 0x412f, 0x0008, 0x516f, 0x0008, 0x61af, 0x0008, 0x3032, 0x002d, 0x0008, 0x3036, 0x002d, 0x0008, 0x000c)

let i = 0;
while(!(halt | error | (i >= 100)))
  let i = i + 1;
  0 1 0 0
  1 1 x x
end while
0 1 0 1
*/

/* Test case if.ne:
clock run error halt

# #include "../cpudef.asm"
# 
# move r1, 2
# move r2, 3
# move r3, 3
# 
# ; skip r-r
# if.ne r2, r2
# error
# 
# ; skip r-i
# if.ne r1, 2
# error
# 
# ; no-skip r-r
# if.ne r2, r1
# jump p1
# error
# p1:
# 
# ; no-skip r-i
# if.ne r2, 2
# jump p2
# error
# p2:
# 
# halt

program(0x1021, 0x2031, 0x3031, 0x226c, 0x0008, 0x10af, 0x0008, 0x216c, 0x002d, 0x0008, 0x20af, 0x002d, 0x0008, 0x000c)

let i = 0;
while(!(halt | error | (i >= 100)))
  let i = i + 1;
  0 1 0 0
  1 1 x x
end while
0 1 0 1
*/

/* Test case if.ge:
clock run error halt

# #include "../cpudef.asm"
# 
# move r1, -1
# move r2, 0
# 
# ; skip r-r
# if.ge r1, r2
# error
# 
# ; skip r-i
# if.ge r1, 0
# error
# 
# ; no-skip r-r
# if.ge r2, r1
# jump p1
# error
# p1:
# 
# ; no-skip r-r equal
# if.ge r2, r2
# jump p2
# error
# p2:
# 
# ; no-skip r-i
# if.ge r2, 0
# jump p3
# error
# p3:
# 
# ; no-skip r-i equal
# if.ge r1, -1
# jump p4
# error
# p4:
# 
# halt

program(0x1ff1, 0x2001, 0x1274, 0x0008, 0x1037, 0x0008, 0x2174, 0x002d, 0x0008, 0x2274, 0x002d, 0x0008, 0x2037, 0x002d, 0x0008, 0x1ff7, 0x002d, 0x0008, 0x000c)

let i = 0;
while(!(halt | error | (i >= 100)))
  let i = i + 1;
  0 1 0 0
  1 1 x x
end while
0 1 0 1
*/

/* Test case if.hs:
clock run error halt

# #include "../cpudef.asm"
# 
# move r1, 0
# move r2, -1 ; 0xffff
# 
# ; skip r-r
# if.hs r1, r2
# error
# 
# ; skip r-i
# if.hs r1, -1
# error
# 
# ; no-skip r-r
# if.hs r2, r1
# jump p1
# error
# p1:
# 
# ; no-skip r-r equal
# if.hs r2, r2
# jump p2
# error
# p2:
# 
# ; no-skip r-i
# if.hs r2, -1
# jump p3
# error
# p3:
# 
# ; no-skip r-i equal
# if.hs r1, 0
# jump p4
# error
# p4:
# 
# halt

program(0x1001, 0x2ff1, 0x127c, 0x0008, 0x1fff, 0x0008, 0x217c, 0x002d, 0x0008, 0x227c, 0x002d, 0x0008, 0x2fff, 0x002d, 0x0008, 0x103f, 0x002d, 0x0008, 0x000c)

let i = 0;
while(!(halt | error | (i >= 100)))
  let i = i + 1;
  0 1 0 0
  1 1 x x
end while
0 1 0 1
*/

/* Test case add:
clock run error halt

# #include "../cpudef.asm"
# 
# move r1, 5
# move r2, 3
# add r1, r2
# add r1, 2
# if.ne r1, 10
# error
# halt

program(0x1051, 0x2031, 0x1240, 0x1083, 0x12af, 0x0008, 0x000c)

let i = 0;
while(!(halt | error | (i >= 100)))
  let i = i + 1;
  0 1 0 0
  1 1 x x
end while
0 1 0 1
*/

/* Test case sub:
clock run error halt

# #include "../cpudef.asm"
# 
# move r1, 5
# move r2, 3
# sub r1, r2
# if.ne r1, 2
#   error
# 
# sub r1, 2
# if.ne r1, 0
#   error
# halt

program(0x1051, 0x2031, 0x1244, 0x10af, 0x0008, 0x1087, 0x102f, 0x0008, 0x000c)

let i = 0;
while(!(halt | error | (i >= 100)))
  let i = i + 1;
  0 1 0 0
  1 1 x x
end while
0 1 0 1
*/

/* Test case xor:
clock run error halt

# #include "../cpudef.asm"
# 
# move r1,  0b110
# move r2,  0b010
# 
# xor r1, r2
# if.ne r1, 0b100
#   error
# 
# xor r1, r2
# if.ne r1, 0b110
#   error
# 
# xor r1,   0b011
# if.ne r1, 0b101
#   error
# 
# halt

program(0x1061, 0x2021, 0x1250, 0x112f, 0x0008, 0x1250, 0x11af, 0x0008, 0x10d3, 0x116f, 0x0008, 0x000c)

let i = 0;
while(!(halt | error | (i >= 100)))
  let i = i + 1;
  0 1 0 0
  1 1 x x
end while
0 1 0 1
*/

/* Test case and:
clock run error halt

# #include "../cpudef.asm"
# 
# move r1,  0b0110
# move r2,  0b1010
# 
# and r1, r2
# if.ne r1, 0b0010
#   error
# 
# and r2,   0b1101
# if.ne r2, 0b1000
#   error
# 
# halt

program(0x1061, 0x20a1, 0x1254, 0x10af, 0x0008, 0x2357, 0x222f, 0x0008, 0x000c)

let i = 0;
while(!(halt | error | (i >= 100)))
  let i = i + 1;
  0 1 0 0
  1 1 x x
end while
0 1 0 1
*/

/* Test case or:
clock run error halt

# #include "../cpudef.asm"
# 
# move r1,  0b0110
# move r2,  0b1010
# 
# or r1, r2
# if.ne r1, 0b1110
#   error
# 
# or r2,   0b0001
# if.ne r2, 0b1011
#   error
# 
# halt

program(0x1061, 0x20a1, 0x1258, 0x13af, 0x0008, 0x205b, 0x22ef, 0x0008, 0x000c)

let i = 0;
while(!(halt | error | (i >= 100)))
  let i = i + 1;
  0 1 0 0
  1 1 x x
end while
0 1 0 1
*/

/* Test case call:
clock run error halt

# #include "../cpudef.asm"
# 
# call test
# if.ne r1, 5
#   error
# halt
# 
# error
# test:
#   move r1, 5
#   jump r0
# 
# error
# halt

program(0x0095, 0x116f, 0x0008, 0x000c, 0x0008, 0x1051, 0x0010, 0x0008, 0x000c)

let i = 0;
while(!(halt | error | (i >= 100)))
  let i = i + 1;
  0 1 0 0
  1 1 x x
end while
0 1 0 1
*/

/* Test case shl:
clock run error halt

# #include "../cpudef.asm"
# 
# move r1,  0b011
# move r2,  0
# move r3,  1
# move r4,  2
# 
# shl r1, 0
# if.ne r1, 0b011
#   error
# 
# shl r1, r2
# if.ne r1, 0b011
#   error
# 
# shl r1, 1
# if.ne r1, 0b110
#   error
# 
# shl r1, r3
# if.ne r1, 0b1100
#   error
# 
# move r1,  0b011
# 
# shl r1, 2
# if.ne r1, 0b1100
#   error
# 
# move r1,  0b011
# 
# shl r1, r4
# if.ne r1, 0b1100
#   error
# 
# halt

program(0x1031, 0x2001, 0x3011, 0x4021, 0x101f, 0x10ef, 0x0008, 0x125c, 0x10ef, 0x0008, 0x105f, 0x11af, 0x0008, 0x135c, 0x132f, 0x0008, 0x1031, 0x109f, 0x132f, 0x0008, 0x1031, 0x145c, 0x132f, 0x0008, 0x000c)

let i = 0;
while(!(halt | error | (i >= 100)))
  let i = i + 1;
  0 1 0 0
  1 1 x x
end while
0 1 0 1
*/

/* Test case shr:
clock run error halt

# #include "../cpudef.asm"
# 
# move r1,  0b110
# move r2,  0
# move r3,  1
# move r4,  2
# 
# shr r1, 0
# if.ne r1, 0b110
#   error
# 
# shr r1, r2
# if.ne r1, 0b110
#   error
# 
# shr r1, 1
# if.ne r1, 0b011
#   error
# 
# shr r1, r3
# if.ne r1, 0b001
#   error
# 
# move r1,  0b1100
# 
# shr r1, 2
# if.ne r1, 0b0011
#   error
# 
# move r1,  0b1100
# 
# shr r1, r4
# if.ne r1, 0b0011
#   error
# 
# move r1, -42
# shr r1, 2
# if.eq r1, -10
#   error
# 
# halt

program(0x1061, 0x2001, 0x3011, 0x4021, 0x1023, 0x11af, 0x0008, 0x1260, 0x11af, 0x0008, 0x1063, 0x10ef, 0x0008, 0x1360, 0x106f, 0x0008, 0x10c1, 0x10a3, 0x10ef, 0x0008, 0x10c1, 0x1460, 0x10ef, 0x0008, 0x1d61, 0x10a3, 0x1dab, 0x0008, 0x000c)

let i = 0;
while(!(halt | error | (i >= 100)))
  let i = i + 1;
  0 1 0 0
  1 1 x x
end while
0 1 0 1
*/

/* Test case asr:
clock run error halt

# #include "../cpudef.asm"
# 
# move r1,  0b110
# move r2,  0
# move r3,  1
# move r4,  2
# 
# asr r1, 0
# if.ne r1, 0b110
#   error
# 
# asr r1, r2
# if.ne r1, 0b110
#   error
# 
# asr r1, 1
# if.ne r1, 0b011
#   error
# 
# asr r1, r3
# if.ne r1, 0b001
#   error
# 
# move r1,  0b1100
# 
# asr r1, 2
# if.ne r1, 0b0011
#   error
# 
# move r1,  0b1100
# 
# asr r1, r4
# if.ne r1, 0b0011
#   error
# 
# move r1, -8
# asr r1, 2
# if.ne r1, -2
#   error
# 
# asr r1, 2
# if.ne r1, -1
#   error
# 
# move r1, -10
# asr r1, 1
# if.ne r1, -5
#   error
# 
# halt

program(0x1061, 0x2001, 0x3011, 0x4021, 0x1027, 0x11af, 0x0008, 0x1264, 0x11af, 0x0008, 0x1067, 0x10ef, 0x0008, 0x1364, 0x106f, 0x0008, 0x10c1, 0x10a7, 0x10ef, 0x0008, 0x10c1, 0x1464, 0x10ef, 0x0008, 0x1f81, 0x10a7, 0x1faf, 0x0008, 0x10a7, 0x1fef, 0x0008, 0x1f61, 0x1067, 0x1eef, 0x0008, 0x000c)

let i = 0;
while(!(halt | error | (i >= 100)))
  let i = i + 1;
  0 1 0 0
  1 1 x x
end while
0 1 0 1
*/
