// Digital circuit framebuffer.dig as structural Verilog
module framebuffer (
  input  clk,
  input  [11:0] x,
  input  [11:0] y,
  input  [7:0] r,
  input  [7:0] g,
  input  [7:0] b
);

  wire [15:15] Frame_Buffer_d;
  wire [18:0] add_1_s;
  wire [23:0] mul_1_mul;

  Mul #(.Bits(12)) mul_1 (.a(y), .b(12'h280), .mul(mul_1_mul));
  Add #(.Bits(19)) add_1 (.a({{7{1'b0}}, x}), .b(mul_1_mul[18:0]), .c_i(1'b0), .s(add_1_s));  // open: c_o
  GraphicCard #(.graphicHeight(360), .graphicWidth(640), .Bits(16)) Frame_Buffer (
    .A(add_1_s), .str(1'b1), .C(clk), .ld(1'b0), .B(1'b0), .D({Frame_Buffer_d[15], b[7:3], g[7:3], r[7:3]}));
  // also tied to VCC on the sheet: Frame_Buffer_d[15]

  // Notes on the sheet:
  //   8:8:8 RGB -> 5:5:5 RGB
endmodule
