// Digital circuit maxcounter.dig as structural Verilog
module maxcounter (
  input  en,
  input  C,
  input  max,
  input  rst,
  output Q,
  output ovf,
  output N
);

  wire multiplexer_1_out, or_1_out;

  or or_1 (or_1_out, ovf, rst);
  Multiplexer #(.generic("this.Bits = args.bitWidth;")) multiplexer_1 (
    .sel(or_1_out), .in_0(N), .in_1(1'b0), .out(multiplexer_1_out));
  Register #(.generic("this.Bits = args.bitWidth;")) register_1 (.D(multiplexer_1_out), .C(C), .en(en), .Q(Q));
  plusone #(.generic("bitWidth := args.bitWidth;")) plusone_1 (.A(Q), .Y(N));
  equals #(.generic("bitWidth := args.bitWidth;")) equals_1 (.A(N), .B(max), .Q(ovf));

  // Notes on the sheet:
  //   max: default 5
endmodule

/* Code that sets the parameters or builds the circuit:
bitWidth := 8;
*/
