// Digital circuit palettebram.dig as structural Verilog
module palettebram (
  input  [8:0] pixel,
  input  pal_we,
  input  [9:0] pal_adr,
  input  [15:0] pal_dat,
  input  clk,
  input  rst,
  output [23:0] colour
);

  wire and_1_out, and_2_out, paletteboot_1_we_o;
  wire [7:0] PalBRAM2_d2;
  wire [9:0] paletteboot_1_adr_o;
  wire [15:0] PalBRAM1_d2, paletteboot_1_dat_o;

  paletteboot paletteboot_1 (
    .we_i(pal_we), .adr_i(pal_adr), .dat_i(pal_dat), .clk(clk), .rst(rst), .we_o(paletteboot_1_we_o),
    .adr_o(paletteboot_1_adr_o), .dat_o(paletteboot_1_dat_o));
  and and_1 (and_1_out, paletteboot_1_we_o, ~paletteboot_1_adr_o[0]);  // And
  and and_2 (and_2_out, paletteboot_1_we_o, paletteboot_1_adr_o[0]);
  RAMDualAccess #(.AddrBits(9), .Bits(16)) PalBRAM1 (
    .str(and_1_out), .C(clk), .ld(1'b0), .A1(paletteboot_1_adr_o[9:1]), .Din1(paletteboot_1_dat_o),
    .A2(pixel), .D2(PalBRAM1_d2));  // open: D1
  RAMDualAccess #(.AddrBits(9), .Bits(8)) PalBRAM2 (
    .str(and_2_out), .C(clk), .ld(1'b0), .A1(paletteboot_1_adr_o[9:1]), .Din1(paletteboot_1_dat_o[7:0]),
    .A2(pixel), .D2(PalBRAM2_d2));  // open: D1
  D_FF #(.Bits(24)) d_ff_1 (.D({PalBRAM2_d2, PalBRAM1_d2}), .C(clk), .Q(colour));  // open: nQ

  // Other names for the same wires on the sheet: C = clk; R = rst

  // Notes on the sheet:
  //   clk: Hz: 50
endmodule
