// Digital circuit scanxy.dig as structural Verilog
module scanxy (
  input  C,
  input  rst,
  input  en,
  input  [11:0] hr,
  input  [11:0] vr,
  output [11:0] nx,
  output [11:0] ny,
  output [11:0] x,
  output [11:0] y,
  output nl,
  output nf
);

  wire X_ovf, Y_ovf;

  and and_1 (nl, X_ovf, en);
  maxcounter #(.generic("bitWidth := 12;")) u_X (.en(en), .C(C), .max(hr), .rst(rst), .Q(x), .ovf(X_ovf), .N(nx));
  maxcounter #(.generic("bitWidth := 12;")) u_Y (.en(nl), .C(C), .max(vr), .rst(rst), .Q(y), .ovf(Y_ovf), .N(ny));
  and and_2 (nf, nl, Y_ovf);

  // Other names for the same wires on the sheet: R = rst

  // Notes on the sheet:
  //   hr: default 5
  //   vr: default 3
endmodule
