// Digital circuit sync.dig as structural Verilog
module sync (
  input  clk,
  input  rst,
  input  [11:0] v,
  input  [11:0] fp,
  input  [11:0] sync,
  input  [11:0] bp,
  input  n,
  input  neg,
  output blank,
  output pulse
);

  wire equals_1_q, equals_2_q, equals_3_q, or_1_out, or_2_out, rsff_2_nq, rsff_2_q;

  equals #(.generic("bitWidth := 12;")) equals_1 (.A(v), .B(fp), .Q(equals_1_q));
  equals #(.generic("bitWidth := 12;")) equals_2 (.A(v), .B(sync), .Q(equals_2_q));
  equals #(.generic("bitWidth := 12;")) equals_3 (.A(v), .B(bp), .Q(equals_3_q));
  or or_1 (or_1_out, rst, n);
  or or_2 (or_2_out, rst, equals_3_q);
  rsff rsff_1 (.S(equals_1_q), .C(clk), .R(or_1_out), .Q(blank));  // open: nQ
  rsff rsff_2 (.S(equals_2_q), .C(clk), .R(or_2_out), .Q(rsff_2_q), .nQ(rsff_2_nq));
  Multiplexer multiplexer_1 (.sel(neg), .in_0(rsff_2_q), .in_1(rsff_2_nq), .out(pulse));

  // Other names for the same wires on the sheet: C = clk; R = rst

  // Notes on the sheet:
  //   fp: default 3
  //   sync: default 5
  //   bp: default 7
endmodule
