// Digital circuit top_simfb.dig as structural Verilog
module top_simfb (
  input  clk,
  input  rst
);

  wire scanxy_1_frame, scanxy_1_line;
  wire [7:0] engine_1_b, engine_1_g, engine_1_r;
  wire [11:0] engine_1_x_o, engine_1_y_o, scanxy_1_x, scanxy_1_y;

  scanxy scanxy_1 (
    .C(clk), .rst(rst), .en(1'b1), .h_total(12'h280), .v_total(12'h168), .x(scanxy_1_x), .y(scanxy_1_y),
    .line(scanxy_1_line), .frame(scanxy_1_frame));
  engine engine_1 (
    .x_i(scanxy_1_x), .y_i(scanxy_1_y), .line(scanxy_1_line), .frame(scanxy_1_frame), .hsync_i(1'b0),
    .vsync_i(1'b0), .en_disp_i(1'b1), .clk(clk), .rst(rst), .x_o(engine_1_x_o), .y_o(engine_1_y_o),
    .r(engine_1_r), .g(engine_1_g), .b(engine_1_b));  // open: hsync_o, vsync_o, en_disp_o
  framebuffer framebuffer_1 (
    .x(engine_1_x_o), .y(engine_1_y_o), .r(engine_1_r), .g(engine_1_g), .b(engine_1_b), .clk(clk));

  // Other names for the same wires on the sheet: C = clk; R = rst

  // Notes on the sheet:
  //   clk: Hz: 2147483647
endmodule
