// Digital circuit top_simvga.dig as structural Verilog
module top_simvga (
  input  clk,
  input  rst
);

  wire vdp_1_hs, vdp_1_vs;
  wire [7:0] vdp_1_b, vdp_1_g, vdp_1_r;

  vdp vdp_1 (
    .clk(clk), .rst(rst), .hfp(12'h280), .hsn(12'h290), .hbp(12'h2f0), .httl(12'h320), .hneg(1'b1),
    .vfp(12'h168), .vsn(12'h19c), .vbp(12'h19e), .vttl(12'h1c1), .vneg(1'b0), .R(vdp_1_r), .G(vdp_1_g),
    .B(vdp_1_b), .hs(vdp_1_hs), .vs(vdp_1_vs));  // open: de, X, Y, nl, nf
  VGA vga_1 (.R(vdp_1_r), .G(vdp_1_g), .B(vdp_1_b), .H(vdp_1_hs), .V(vdp_1_vs), .C(clk));

  // Other names for the same wires on the sheet: C = clk; R = rst

  // Notes on the sheet:
  //   clk: Hz: 2147483647
endmodule
