// Digital circuit vdp.dig as structural Verilog
module vdp (
  input  clk,
  input  rst,
  input  [11:0] hfp,
  input  [11:0] hsn,
  input  [11:0] hbp,
  input  [11:0] httl,
  input  hneg,
  input  [11:0] vfp,
  input  [11:0] vsn,
  input  [11:0] vbp,
  input  [11:0] vttl,
  input  vneg,
  output [7:0] R,
  output [7:0] G,
  output [7:0] B,
  output hs,
  output vs,
  output de,
  output [11:0] X,
  output [11:0] Y,
  output nl,
  output nf
);

  wire scanxy_1_nf, scanxy_1_nl, vgasync_1_de, vgasync_1_hs, vgasync_1_nf_o, vgasync_1_nl_o, vgasync_1_vs;
  wire [11:0] scanxy_1_x, scanxy_1_y, vgasync_1_x_o, vgasync_1_y_o;

  scanxy scanxy_1 (
    .C(clk), .rst(rst), .en(1'b1), .hr(httl), .vr(vttl), .X(scanxy_1_x), .Y(scanxy_1_y), .nl(scanxy_1_nl),
    .nf(scanxy_1_nf));
  vgasync vgasync_1 (
    .clk(clk), .rst(rst), .X_i(scanxy_1_x), .Y_i(scanxy_1_y), .nl_i(scanxy_1_nl), .nf_i(scanxy_1_nf),
    .hfp(hfp), .hsn(hsn), .hbp(hbp), .hneg(hneg), .vfp(vfp), .vsn(vsn), .vbp(vbp), .vneg(vneg),
    .X_o(vgasync_1_x_o), .Y_o(vgasync_1_y_o), .nl_o(vgasync_1_nl_o), .nf_o(vgasync_1_nf_o),
    .hs(vgasync_1_hs), .vs(vgasync_1_vs), .de(vgasync_1_de));
  engine engine_1 (
    .clk(clk), .rst(rst), .x_i(vgasync_1_x_o), .y_i(vgasync_1_y_o), .nl_i(vgasync_1_nl_o),
    .nf_i(vgasync_1_nf_o), .hs_i(vgasync_1_hs), .vs_i(vgasync_1_vs), .de_i(vgasync_1_de), .x_o(X), .y_o(Y),
    .nl_o(nl), .nf_o(nf), .r(R), .g(G), .b(B), .hs_o(hs), .vs_o(vs), .de_o(de));

  // Other names for the same wires on the sheet: C = clk; R_t = rst

  // Notes on the sheet:
  //   clk: Hz: 2147483647
  //   hfp: default 3
  //   hsn: default 5
  //   hbp: default 5
  //   vfp: default 3
  //   vsn: default 5
  //   vbp: default 5
endmodule
