// Digital circuit vgasync.dig as structural Verilog
module vgasync (
  input  clk,
  input  rst,
  input  [11:0] x_next,
  input  [11:0] y_next,
  input  [11:0] x_i,
  input  [11:0] y_i,
  input  line_i,
  input  frame_i,
  input  [11:0] h_fp,
  input  [11:0] h_sync,
  input  [11:0] h_bp,
  input  h_neg,
  input  [11:0] v_fp,
  input  [11:0] v_sync,
  input  [11:0] v_bp,
  input  v_neg,
  output [11:0] x_o,
  output [11:0] y_o,
  output line_o,
  output frame_o,
  output hsync,
  output vsync,
  output en_disp
);

  wire H_blank, V_blank;

  sync H (
    .clk(clk), .rst(rst), .en(1'b1), .v(x_next), .fp(h_fp), .sync(h_sync), .bp(h_bp), .n(line_i),
    .neg(h_neg), .blank(H_blank), .pulse(hsync));
  sync V (
    .clk(clk), .rst(rst), .en(line_i), .v(y_next), .fp(v_fp), .sync(v_sync), .bp(v_bp), .n(frame_i),
    .neg(v_neg), .blank(V_blank), .pulse(vsync));
  nor nor_1 (en_disp, H_blank, V_blank);

  assign frame_o = frame_i;
  assign line_o = line_i;
  assign x_o = x_i;
  assign y_o = y_i;

  // Other names for the same wires on the sheet: C = clk; frame_t = frame_i; line_t = line_i; R = rst

  // Notes on the sheet:
  //   h_fp: default 3
  //   h_sync: default 5
  //   h_bp: default 5
  //   v_fp: default 3
  //   v_sync: default 5
  //   v_bp: default 5
endmodule
