// Digital circuit vga_aluopdisp.dig as structural Verilog
module vga_aluopdisp (
  input  [7:0] CX_i,
  input  [7:0] CY_i,
  input  [6:0] C_i,
  input  [11:0] fg_i,
  input  [11:0] bg_i,
  input  [11:0] fg_c,
  input  [11:0] bg_c,
  input  [5:0] CX_c,
  input  [7:0] CY_c,
  input  en,
  input  [2:0] aop,
  output [7:0] CX_o,
  output [7:0] CY_o,
  output [6:0] C_o,
  output [11:0] fg_o,
  output [11:0] bg_o,
  output busy,
  output L_v,
  output R_v,
  output res_v
);

  wire [6:0] aluop2ascii_1_l0, aluop2ascii_1_l1, aluop2ascii_1_l2, aluop2ascii_1_l3;

  aluop2ascii aluop2ascii_1 (
    .I({1'b0, aop}), .L0(aluop2ascii_1_l0), .L1(aluop2ascii_1_l1), .L2(aluop2ascii_1_l2),
    .L3(aluop2ascii_1_l3), .L_v(L_v), .R_v(R_v), .res_v(res_v));
  // vga_string vga_string_1: pin names not known; wires that end beside it: CX_i, CY_i, C_i, fg_i, bg_i, fg_c, bg_c, CX_c, CY_c, aluop2ascii_1_l0, aluop2ascii_1_l1, aluop2ascii_1_l2, aluop2ascii_1_l3, en, CX_o, CY_o, C_o, fg_o, bg_o, busy
endmodule
