// Digital circuit vga_charpos.dig as structural Verilog
module vga_charpos (
  input  [11:0] X,
  input  [11:0] Y,
  output [4:0] row,
  output [3:0] col,
  output [7:0] CX,
  output [7:0] CY
);

  BitExtender #(.inputBits(12), .outputBits(13)) bitextender_1 (.in(Y), .out({CY, row}));

  assign col = X[3:0];
  assign CX = X[11:4];
endmodule
