// Digital circuit vga_display.dig as structural Verilog
module vga_display (
  input  clock,
  input  [15:0] CD,
  output [3:0] R,
  output [3:0] G,
  output [3:0] B,
  output hs,
  output vs,
  output de,
  output [10:0] CA
);

  wire vga_sync_1_h, vga_sync_1_pic, vga_sync_1_v;
  wire [3:0] vga_charpos_1_col;
  wire [4:0] vga_charpos_1_row;
  wire [6:0] vga_hex_1_c_o, vga_string_1_c_o, vga_string_2_c_o, vga_string_3_c_o;
  wire [7:0] vga_charpos_1_cx, vga_charpos_1_cy, vga_string_1_cx_o, vga_string_1_cy_o, vga_string_2_cx_o,
       vga_string_2_cy_o, vga_string_3_cx_o, vga_string_3_cy_o;
  wire [11:0] vga_hex_1_bg_o, vga_hex_1_fg_o, vga_string_1_bg_o, vga_string_1_fg_o, vga_string_2_bg_o,
       vga_string_2_fg_o, vga_string_3_bg_o, vga_string_3_fg_o;
  wire [15:0] register_1_q, vga_sync_1_x, vga_sync_1_y;
  wire [31:0] counter_1_out;

  vga_sync vga_sync_1 (
    .clock(clock), .H(vga_sync_1_h), .V(vga_sync_1_v), .pic(vga_sync_1_pic), .X(vga_sync_1_x),
    .Y(vga_sync_1_y));
  vga_charpos vga_charpos_1 (
    .X(vga_sync_1_x), .Y(vga_sync_1_y), .row(vga_charpos_1_row), .col(vga_charpos_1_col),
    .CX(vga_charpos_1_cx), .CY(vga_charpos_1_cy));
  vga_string vga_string_1 (
    .CX_i(vga_charpos_1_cx), .CY_i(vga_charpos_1_cy), .C_i({7{1'b0}}), .fg_i({12{1'b0}}), .bg_i({12{1'b0}}),
    .fg_c(12'he07), .bg_c(12'h222), .CX_c(6'b000011), .CY_c(8'h7), .C_0(7'b1001000), .C_1(7'b1000101),
    .C_2(7'b1001100), .C_3(7'b1001100), .en(1'b1), .CX_o(vga_string_1_cx_o), .CY_o(vga_string_1_cy_o),
    .C_o(vga_string_1_c_o), .fg_o(vga_string_1_fg_o), .bg_o(vga_string_1_bg_o));
  vga_string vga_string_2 (
    .CX_i(vga_string_1_cx_o), .CY_i(vga_string_1_cy_o), .C_i(vga_string_1_c_o), .fg_i(vga_string_1_fg_o),
    .bg_i(vga_string_1_bg_o), .fg_c(12'he07), .bg_c(12'h222), .CX_c(6'b000100), .CY_c(8'h7),
    .C_0(7'b1001111), .C_1(7'b0100000), .C_2(7'b1010111), .C_3(7'b1001111), .en(1'b1),
    .CX_o(vga_string_2_cx_o), .CY_o(vga_string_2_cy_o), .C_o(vga_string_2_c_o), .fg_o(vga_string_2_fg_o),
    .bg_o(vga_string_2_bg_o));
  Counter #(.Bits(32)) counter_1 (.en(1'b1), .C(clock), .clr(1'b0), .out(counter_1_out));  // open: ovf
  vga_string vga_string_3 (
    .CX_i(vga_string_2_cx_o), .CY_i(vga_string_2_cy_o), .C_i(vga_string_2_c_o), .fg_i(vga_string_2_fg_o),
    .bg_i(vga_string_2_bg_o), .fg_c(12'he07), .bg_c(12'h222), .CX_c(6'b000101), .CY_c(8'h7),
    .C_0(7'b1010010), .C_1(7'b1001100), .C_2(7'b1000100), .C_3(7'b0100001), .en(1'b1),
    .CX_o(vga_string_3_cx_o), .CY_o(vga_string_3_cy_o), .C_o(vga_string_3_c_o), .fg_o(vga_string_3_fg_o),
    .bg_o(vga_string_3_bg_o));
  Register #(.Bits(16)) register_1 (.D(counter_1_out[31:16]), .C(clock), .en(~de), .Q(register_1_q));
  vga_hex vga_hex_1 (
    .CX_i(vga_string_3_cx_o), .CY_i(vga_string_3_cy_o), .C_i(vga_string_3_c_o), .fg_i(vga_string_3_fg_o),
    .bg_i(vga_string_3_bg_o), .fg_c(12'h1be), .bg_c(12'h222), .CX_c(6'b000100), .CY_c(8'h8),
    .N(register_1_q), .en(1'b1), .C_o(vga_hex_1_c_o), .fg_o(vga_hex_1_fg_o), .bg_o(vga_hex_1_bg_o));  // open: CX_o, CY_o
  vga_text vga_text_1 (
    .H_i(vga_sync_1_h), .V_i(vga_sync_1_v), .pic(vga_sync_1_pic), .row(vga_charpos_1_row),
    .col(vga_charpos_1_col), .CD(CD), .clock(clock), .char(vga_hex_1_c_o), .fg(vga_hex_1_fg_o),
    .bg(vga_hex_1_bg_o), .R(R), .G(G), .B(B), .hs(hs), .vs(vs), .de(de), .CA(CA));

  // Other names for the same wires on the sheet: C = clock

  // Notes on the sheet:
  //   clock: Hz: 2147483647
endmodule
