// Digital circuit vga_labelnum.dig as structural Verilog
module vga_labelnum (
  input  [7:0] CX_i,
  input  [7:0] CY_i,
  input  [6:0] C_i,
  input  [3:0] fg_i,
  input  [3:0] fg_lab,
  input  [3:0] fg_num,
  input  [4:0] CX_c,
  input  [7:0] CY_c,
  input  en,
  input  [6:0] L_0,
  input  [6:0] L_1,
  input  [6:0] L_2,
  input  [15:0] N,
  output [7:0] CX_o,
  output [7:0] CY_o,
  output [6:0] C_o,
  output [3:0] fg_o
);

  wire [3:0] Label_fg_o;
  wire [6:0] Label_c_o;
  wire [7:0] Label_cx_o, Label_cy_o;

  vga_string Label (
    .CX_i(CX_i), .CY_i(CY_i), .C_i(C_i), .fg_i(fg_i), .fg_c(fg_lab), .CX_c({CX_c, 1'b0}), .CY_c(CY_c),
    .C_0(L_0), .C_1(L_1), .C_2(L_2), .C_3(7'b0100000), .en(en), .CX_o(Label_cx_o), .CY_o(Label_cy_o),
    .C_o(Label_c_o), .fg_o(Label_fg_o));
  vga_hex Num (
    .CX_i(Label_cx_o), .CY_i(Label_cy_o), .C_i(Label_c_o), .fg_i(Label_fg_o), .fg_c(fg_num),
    .CX_c({CX_c, 1'b1}), .CY_c(CY_c), .N(N), .en(en), .CX_o(CX_o), .CY_o(CY_o), .C_o(C_o), .fg_o(fg_o));
endmodule
