// Digital circuit vga_opdisp.dig as structural Verilog
module vga_opdisp (
  input  [7:0] CX_i,
  input  [7:0] CY_i,
  input  [6:0] C_i,
  input  [3:0] fg_i,
  input  [3:0] fg_c,
  input  [4:0] CX_c,
  input  [7:0] CY_c,
  input  en,
  input  [4:0] op,
  input  [2:0] cond,
  output [7:0] CX_o,
  output [7:0] CY_o,
  output [6:0] C_o,
  output [3:0] fg_o
);

  wire [3:0] H1_p16;
  wire [6:0] H1_p15, op2ascii_1_l0, op2ascii_1_l1, op2ascii_1_l2, op2ascii_1_l3, op2ascii_1_l4, op2ascii_1_l5;
  wire [7:0] H1_p13, H1_p14;

  op2ascii op2ascii_1 (
    .I(op), .C(cond), .L0(op2ascii_1_l0), .L1(op2ascii_1_l1), .L2(op2ascii_1_l2), .L3(op2ascii_1_l3),
    .L4(op2ascii_1_l4), .L5(op2ascii_1_l5));
  // vga_string H1: pin names not known; wires that end beside it: CX_i, CY_i, C_i, fg_i, fg_c, {CX_c, 1'b0}, CY_c, 7'b0100000, op2ascii_1_l0, op2ascii_1_l1, op2ascii_1_l2, en, H1_p13, H1_p14, H1_p15, H1_p16
  vga_string H2 (
    .CX_i(H1_p13), .CY_i(H1_p14), .C_i(H1_p15), .fg_i(H1_p16), .fg_c(fg_c), .CX_c({CX_c, 1'b1}), .CY_c(CY_c),
    .C_0(op2ascii_1_l3), .C_1(op2ascii_1_l4), .C_2(op2ascii_1_l5), .C_3(7'b0100000), .en(en), .CX_o(CX_o),
    .CY_o(CY_o), .C_o(C_o), .fg_o(fg_o));
endmodule
