// Digital circuit vga_regdisp.dig as structural Verilog
module vga_regdisp (
  input  [7:0] CX_i,
  input  [7:0] CY_i,
  input  [6:0] C_i,
  input  [11:0] fg_i,
  input  [11:0] bg_i,
  input  [11:0] fg_c,
  input  [11:0] bg_c,
  input  [5:0] CX_c,
  input  [7:0] CY_c,
  input  en,
  input  [3:0] R,
  input  J,
  input  [6:0] sep,
  output [7:0] CX_o,
  output [7:0] CY_o,
  output [6:0] C_o,
  output [11:0] fg_o,
  output [11:0] bg_o,
  output busy
);

  wire [6:0] reg2ascii_1_d_0, reg2ascii_1_d_1, reg2ascii_1_d_2;

  reg2ascii reg2ascii_1 (.R(R), .J(J), .D_0(reg2ascii_1_d_0), .D_1(reg2ascii_1_d_1), .D_2(reg2ascii_1_d_2));
  // vga_string vga_string_1: pin names not known; wires that end beside it: CX_i, CY_i, C_i, fg_i, bg_i, fg_c, bg_c, CX_c, CY_c, reg2ascii_1_d_0, reg2ascii_1_d_1, reg2ascii_1_d_2, sep, en, CX_o, CY_o, C_o, fg_o, bg_o, busy
endmodule
