// Digital circuit vga_sync.dig as structural Verilog
module vga_sync (
  input  clock,
  output H,
  output V,
  output pic,
  output [15:0] X,
  output [15:0] Y
);

  wire comparator_1_lt, comparator_2_lt, Horiz_next;

  vga_timing Horiz (
    .en(1'b1), .clock(clock), .res(16'h280), .fp(16'h10), .sync(16'h60), .bp(16'h30), .neg(1'b1), .V(X),
    .pulse(H), .next(Horiz_next));
  vga_timing Vert (
    .en(Horiz_next), .clock(clock), .res(16'h1e0), .fp(16'hb), .sync(16'h2), .bp(16'h21), .neg(1'b1), .V(Y),
    .pulse(V));  // open: next
  Comparator #(.Bits(16)) comparator_1 (.a(X), .b(16'h280), .lt(comparator_1_lt));  // open: gt, eq
  Comparator #(.Bits(16)) comparator_2 (.a(Y), .b(16'h1e0), .lt(comparator_2_lt));  // open: gt, eq
  and and_1 (pic, comparator_1_lt, comparator_2_lt);

  // Other names for the same wires on the sheet: C = clock
endmodule
