// Digital circuit bin2bcd.dig as structural Verilog
module bin2bcd (
  input  [15:0] in_1,
  input  clock_b2b
);

  wire and_1_out, button_1_out, counterpreset_1_ovf, d_ff_as_1_nq, or_1_out;
  wire [3:0] counterpreset_1_out, d_ff_as_2_q, d_ff_as_2_q_2, d_ff_as_2_q_3, d_ff_as_2_q_4, d_ff_as_2_q_5;
  wire [3:3] gt4add3_1_o;
  wire [19:0] bitselector_1_out;

  Button button_1 (.out(button_1_out));
  D_FF_AS d_ff_as_1 (
    .Set(1'b0), .D(counterpreset_1_ovf), .C(and_1_out), .Clr(button_1_out), .nQ(d_ff_as_1_nq));  // open: Q
  or or_1 (or_1_out, button_1_out, and_1_out);
  and and_1 (and_1_out, d_ff_as_1_nq, clock_b2b, ~counterpreset_1_ovf);  // And
  BitSelector #(.Selector_Bits(4)) bitselector_1 (.in(in_1), .sel(counterpreset_1_out), .out(bitselector_1_out[0]));
  LED led_1 (.in(bitselector_1_out[0]));
  CounterPreset #(.Bits(4)) counterpreset_1 (
    .en(1'b1), .C(or_1_out), .dir(1'b1), .in(4'b1111), .ld(button_1_out), .clr(1'b0),
    .out(counterpreset_1_out), .ovf(counterpreset_1_ovf));
  Seven_Seg_Hex seven_seg_hex_1 (.d(bitselector_1_out[19:16]), .dp(1'b0));
  gt4add3 gt4add3_1 (.I(d_ff_as_2_q_5), .O({gt4add3_1_o[3], bitselector_1_out[19:17]}));
  Seven_Seg_Hex seven_seg_hex_2 (.d(bitselector_1_out[15:12]), .dp(1'b0));
  gt4add3 gt4add3_2 (.I(d_ff_as_2_q_4), .O(bitselector_1_out[16:13]));
  D_FF_AS #(.Bits(20)) d_ff_as_2 (
    .Set(1'b0), .D(bitselector_1_out), .C(and_1_out), .Clr(button_1_out),
    .Q({d_ff_as_2_q_5, d_ff_as_2_q_4, d_ff_as_2_q_3, d_ff_as_2_q_2, d_ff_as_2_q}));  // open: nQ
  Seven_Seg_Hex seven_seg_hex_3 (.d(bitselector_1_out[11:8]), .dp(1'b0));
  gt4add3 gt4add3_3 (.I(d_ff_as_2_q_3), .O(bitselector_1_out[12:9]));
  Seven_Seg_Hex seven_seg_hex_4 (.d(bitselector_1_out[7:4]), .dp(1'b0));
  gt4add3 gt4add3_4 (.I(d_ff_as_2_q_2), .O(bitselector_1_out[8:5]));
  Seven_Seg_Hex seven_seg_hex_5 (.d(bitselector_1_out[3:0]), .dp(1'b0));
  gt4add3 gt4add3_5 (.I(d_ff_as_2_q), .O(bitselector_1_out[4:1]));

  // Notes on the sheet:
  //   in_1: default 412597816
  //   clock_b2b: Hz: 5
endmodule
