// Digital circuit fpga101.dig as structural Verilog
module fpga101 (
  input  rx,
  input  rst,
  input  clk,
  output tx
);

  wire fsm_1_tx_rd, fsm_1_tx_start, rx_empty, TX_empty, uart_1_rx_ready, uart_1_tx_busy, xfer;
  wire [7:0] QD, TX_q, uart_1_rx_data;

  fifo u_TX (.rd(fsm_1_tx_rd), .wr(xfer), .D(QD), .clk(clk), .clr(rst), .Q(TX_q), .empty(TX_empty));  // open: full
  uart uart_1 (
    .rx(rx), .clk(clk), .tx_start(fsm_1_tx_start), .tx_data(TX_q), .tx(tx), .rx_ready(uart_1_rx_ready),
    .rx_data(uart_1_rx_data), .tx_busy(uart_1_tx_busy));
  fsm fsm_1 (
    .rx_data(uart_1_rx_data), .tx_busy(uart_1_tx_busy), .tx_empty(TX_empty), .clk(clk), .rx_empty(rx_empty),
    .xfer(xfer), .tx_start(fsm_1_tx_start), .tx_rd(fsm_1_tx_rd));
  fifo u_RX (
    .rd(xfer), .wr(uart_1_rx_ready), .D(uart_1_rx_data), .clk(clk), .clr(rst), .Q(QD), .empty(rx_empty));  // open: full

  // Other names for the same wires on the sheet: C = clk; R = rst

  // Notes on the sheet:
  //   clk: Hz: 10
endmodule
